// Logisim project ALU_16BIT.circ as structural Verilog: 1 circuit, main circuit ALU
module ALU (
  input  [4:0] OPCODE,
  input  [15:0] OPERAND_1,
  input  [15:0] OPERAND_2,
  output [15:0] DATA_OUT
);

  wire or_1_out, or_3_out, or_4_out, or_5_out, or_6_out, or_7_out, or_8_out, or_9_out, or_10_out, or_11_out,
       or_12_out, or_13_out, or_14_out, or_16_out;
  wire [0:0] adder_2_cout, not_2_out, not_3_out, not_4_out, or_15_out, subtractor_3_bout;
  wire [15:0] adder_1_out, and_1_out, not_1_out, or_2_out, subtractor_1_out, subtractor_2_out, xor_1_out,
       xor_2_out;

  assign not_1_out = ~OPERAND_1;  // NOT_Gate not_1, 16 bits wide
  or or_1 (or_1_out, xor_2_out[15], xor_2_out[14]);
  Adder #(.width(16)) adder_1 (.a(OPERAND_1), .b(OPERAND_2), .out(adder_1_out));  // open: cin, cout
  Subtractor #(.width(16)) subtractor_1 (.a(OPERAND_1), .b(OPERAND_2), .out(subtractor_1_out));  // open: bin, bout
  assign and_1_out = OPERAND_1 & OPERAND_2;  // AND_Gate and_1, 16 bits wide
  assign or_2_out = OPERAND_1 | OPERAND_2;  // OR_Gate or_2, 16 bits wide
  assign xor_1_out = OPERAND_1 ^ OPERAND_2;  // XOR_Gate xor_1, 16 bits wide
  assign xor_2_out = OPERAND_1 ^ OPERAND_2;  // XOR_Gate xor_2, 16 bits wide
  or or_3 (or_3_out, xor_2_out[13], xor_2_out[12]);
  or or_4 (or_4_out, or_1_out, or_3_out);
  or or_5 (or_5_out, or_4_out, or_8_out);
  Subtractor #(.width(16)) subtractor_2 (.a({16{1'b1}}), .b(OPERAND_2), .out(subtractor_2_out));  // open: bin, bout
  Subtractor #(.width(16)) subtractor_3 (.a(OPERAND_1), .b(OPERAND_2), .bout(subtractor_3_bout[0]));  // open: out, bin
  or or_6 (or_6_out, xor_2_out[11], xor_2_out[10]);
  or or_7 (or_7_out, xor_2_out[9], xor_2_out[8]);
  or or_8 (or_8_out, or_6_out, or_7_out);
  Adder #(.width(16)) adder_2 (.a(OPERAND_1), .b(subtractor_2_out), .cout(adder_2_cout[0]));  // open: out, cin
  or or_9 (or_9_out, xor_2_out[7], xor_2_out[6]);
  or or_10 (or_10_out, xor_2_out[5], xor_2_out[4]);
  or or_11 (or_11_out, or_9_out, or_10_out);
  or or_12 (or_12_out, or_11_out, or_14_out);
  or or_13 (or_13_out, xor_2_out[3], xor_2_out[2]);
  or or_14 (or_14_out, or_13_out, or_16_out);
  not not_2 (not_2_out[0], or_15_out[0]);
  or or_15 (or_15_out[0], or_12_out, or_5_out);
  not not_3 (not_3_out[0], subtractor_3_bout[0]);
  not not_4 (not_4_out[0], adder_2_cout[0]);
  or or_16 (or_16_out, xor_2_out[1], xor_2_out[0]);
  Multiplexer #(.select(5), .width(16)) multiplexer_1 (
    .in0({16{1'b0}}), .in1(adder_1_out), .in2(subtractor_1_out), .in3({1'b0, OPERAND_1[15:1]}),
    .in4({OPERAND_1[14:0], 1'b0}), .in5(and_1_out), .in6(or_2_out), .in7(xor_1_out), .in8(not_1_out),
    .in9({{15{1'b0}}, not_2_out[0]}), .in10({{15{1'b0}}, or_15_out[0]}),
    .in11({{15{1'b0}}, adder_2_cout[0]}), .in12({{15{1'b0}}, subtractor_3_bout[0]}),
    .in13({{15{1'b0}}, not_3_out[0]}), .in14({{15{1'b0}}, not_4_out[0]}), .in15({16{1'b0}}),
    .in16({16{1'b0}}), .in17({16{1'b0}}), .in18({16{1'b0}}), .in19({16{1'b0}}), .in20({16{1'b0}}),
    .in21({16{1'b0}}), .in22({16{1'b0}}), .in23({16{1'b0}}), .in24({16{1'b0}}), .in25({16{1'b0}}),
    .in26({16{1'b0}}), .in27({16{1'b0}}), .in28({16{1'b0}}), .in29({16{1'b0}}), .in30({16{1'b0}}),
    .in31({16{1'b0}}), .out(DATA_OUT), .sel(OPCODE));
endmodule
