// Logisim project Clock_Kronos.circ as structural Verilog: 1 circuit, main circuit Clock_Kronos
module Clock_Kronos (
  input  CLOCK_FREQUENCY,
  input  CLOCK_ON,
  input  MANUAL,
  input  HALT,
  output CLOCK_OUT
);

  wire and_1_out, and_2_out, and_3_out, and_4_out, not_1_out, not_2_out;

  not not_1 (not_1_out, CLOCK_ON);
  not not_2 (not_2_out, HALT);
  and and_1 (and_1_out, not_1_out, MANUAL);
  and and_2 (and_2_out, CLOCK_FREQUENCY, CLOCK_ON);
  and and_3 (and_3_out, and_2_out, not_2_out);
  and and_4 (and_4_out, and_1_out, not_2_out);
  or or_1 (CLOCK_OUT, and_3_out, and_4_out);
endmodule
