// Logisim project Cycle_Counter.circ as structural Verilog: 1 circuit, main circuit Cycle_Counter
module Cycle_Counter (
  input  [4:0] ADRESS,
  input  CLK,
  input  INSTRUCTION_READY,
  input  RESET,
  output INSTRUCTION_END,
  output INSTRUCTION_STATE_2
);

  wire adress_comparator_4bit_1_output_adress, adress_comparator_4bit_2_output_adress,
       adress_comparator_5bit_1_output_adress, and_1_out, and_2_out, and_3_out, and_4_out, and_6_out,
       d_ff_1_q, d_ff_2_q, d_ff_3_qn, not_1_out, or_1_out;
  wire [3:0] multiplexer_1_out, multiplexer_2_out, multiplexer_3_out, multiplexer_4_out, multiplexer_5_out,
       multiplexer_6_out, register_3_q, register_4_q, subtractor_1_out, subtractor_2_out;
  wire [4:0] register_1_q, register_2_q;

  Register #(.width(5)) register_1 (.D(ADRESS), .en(1'b1), .clk(CLK), .Q(register_1_q), .clr(d_ff_2_q));
  D_Flip_Flop d_ff_1 (.D(INSTRUCTION_READY), .clk(CLK), .Q(d_ff_1_q), .reset(d_ff_2_q));  // open: Qn, preset
  D_Flip_Flop d_ff_2 (.D(RESET), .clk(CLK), .Q(d_ff_2_q), .reset(d_ff_2_q));  // open: Qn, preset
  and and_1 (and_1_out, CLK, d_ff_2_q);
  Multiplexer #(.select(5), .width(4)) multiplexer_1 (
    .in0(4'b0000), .in1(4'b0101), .in2(4'b0001), .in3(4'b0001), .in4(4'b0001), .in5(4'b0001), .in6(4'b0001),
    .in7(4'b0001), .in8(4'b0001), .in9(4'b0001), .in10(4'b0001), .in11(4'b0001), .in12(4'b0001),
    .in13(4'b0001), .in14(4'b0001), .in15(4'b0001), .in16(4'b0001), .in17(4'b0001), .in18(4'b0001),
    .in19(4'b0001), .in20(4'b0011), .in21(4'b0001), .in22(4'b0001), .in23(4'b0001), .in24(4'b0001),
    .in25(4'b0001), .in26(4'b0001), .in27(4'b0001), .in28(4'b0001), .in29(4'b0001), .in30(4'b0001),
    .in31(4'b0001), .out(multiplexer_1_out), .sel(register_1_q));
  and and_2 (and_2_out, d_ff_1_q, adress_comparator_4bit_1_output_adress);
  Multiplexer #(.width(4)) multiplexer_2 (
    .in0(multiplexer_3_out), .in1(multiplexer_1_out), .out(multiplexer_2_out), .sel(and_2_out));
  Multiplexer #(.width(4)) multiplexer_3 (
    .in0(subtractor_1_out), .in1(4'b0000), .out(multiplexer_3_out),
    .sel(adress_comparator_4bit_1_output_adress));
  Register #(.width(5)) register_2 (.D(register_1_q), .en(1'b1), .clk(and_3_out), .Q(register_2_q), .clr(or_1_out));
  and and_3 (and_3_out, CLK, adress_comparator_4bit_1_output_adress, d_ff_1_q);
  Subtractor #(.width(4)) subtractor_1 (
    .a(register_3_q), .b(4'b0000), .out(subtractor_1_out), .bin(1'b1));  // open: bout
  Register #(.width(4)) register_3 (.D(multiplexer_2_out), .en(1'b1), .clk(CLK), .Q(register_3_q), .clr(and_1_out));
  D_Flip_Flop d_ff_3 (.D(and_4_out), .clk(CLK), .Qn(d_ff_3_qn), .reset(d_ff_2_q));  // open: Q, preset
  Adress_Comparator_4bit adress_comparator_4bit_1 (
    .ADRESS(register_3_q), .PHYSICAL_ADRESS(4'b0000), .OUTPUT_ADRESS(adress_comparator_4bit_1_output_adress));
  buf or_1 (or_1_out, and_1_out);  // OR_Gate
  Adress_Comparator_5bit adress_comparator_5bit_1 (
    .ADRESS(register_2_q), .PHYSICAL_ADRESS({5{1'b0}}), .OUTPUT_ADRESS(adress_comparator_5bit_1_output_adress));
  and and_4 (and_4_out, not_1_out, adress_comparator_4bit_1_output_adress);
  and and_5 (INSTRUCTION_END, d_ff_3_qn, and_4_out);
  not not_1 (not_1_out, adress_comparator_5bit_1_output_adress);
  Multiplexer #(.select(5), .width(4)) multiplexer_4 (
    .in0(4'b1111), .in1(4'b1111), .in2(4'b1111), .in3(4'b1111), .in4(4'b1111), .in5(4'b1111), .in6(4'b1111),
    .in7(4'b1111), .in8(4'b1111), .in9(4'b1111), .in10(4'b1111), .in11(4'b1111), .in12(4'b1111),
    .in13(4'b1111), .in14(4'b1111), .in15(4'b1111), .in16(4'b0001), .in17(4'b0001), .in18(4'b1111),
    .in19(4'b1111), .in20(4'b0010), .in21(4'b0001), .in22(4'b0001), .in23(4'b1111), .in24(4'b1111),
    .in25(4'b1111), .in26(4'b1111), .in27(4'b1111), .in28(4'b1111), .in29(4'b1111), .in30(4'b1111),
    .in31(4'b1111), .out(multiplexer_4_out), .sel(register_1_q));
  Multiplexer #(.width(4)) multiplexer_5 (
    .in0(subtractor_2_out), .in1(4'b0000), .out(multiplexer_5_out),
    .sel(adress_comparator_4bit_2_output_adress));
  Multiplexer #(.width(4)) multiplexer_6 (
    .in0(multiplexer_5_out), .in1(multiplexer_4_out), .out(multiplexer_6_out), .sel(and_2_out));
  Register #(.width(4)) register_4 (.D(multiplexer_6_out), .en(1'b1), .clk(CLK), .Q(register_4_q), .clr(and_1_out));
  Subtractor #(.width(4)) subtractor_2 (
    .a(register_4_q), .b(4'b0000), .out(subtractor_2_out), .bin(1'b1));  // open: bout
  and and_6 (and_6_out, not_1_out, adress_comparator_4bit_2_output_adress);
  and and_7 (INSTRUCTION_STATE_2, d_ff_3_qn, and_6_out);
  Adress_Comparator_4bit adress_comparator_4bit_2 (
    .ADRESS(register_4_q), .PHYSICAL_ADRESS(4'b0000), .OUTPUT_ADRESS(adress_comparator_4bit_2_output_adress));
endmodule
