// Logisim project Indirect_Adressing_Unit.circ as structural Verilog: 1 circuit, main circuit Indirect_Adressing_Unit
module Indirect_Adressing_Unit (
  input  RESET,
  input  CLK,
  input  [15:0] DATA_0,
  input  [15:0] DATA_1,
  input  [15:0] DATA_2,
  input  INSTRUCTION_READY_IN,
  input  [15:0] INPUT_REG,
  input  [15:0] INPUT_RAM,
  output [15:0] OUTPUT_0,
  output [15:0] OUTPUT_1,
  output [15:0] OUTPUT_2,
  output INSTRUCTION_READY_OUT,
  output [4:0] REG_ADRESS,
  output [14:0] RAM_ADRESS,
  output READ_RAM
);

  wire adress_comparator_4bit_1_output_adress, adress_comparator_4bit_2_output_adress,
       adress_comparator_4bit_3_output_adress, and_1_out, and_2_out, and_3_out, and_4_out, and_5_out,
       and_6_out, and_7_out, and_8_out, and_9_out, and_11_out, and_12_out, and_13_out, and_14_out,
       and_15_out, and_16_out, and_17_out, and_18_out, and_19_out, and_20_out, and_21_out, and_22_out,
       and_23_out, and_24_out, and_25_out, and_26_out, d_ff_1_q, d_ff_2_q, d_ff_3_q, d_ff_3_qn, d_ff_4_q,
       d_ff_5_q, d_ff_6_q, d_ff_7_q, d_ff_8_q, d_ff_8_qn, d_ff_9_q, d_ff_10_q, d_ff_10_qn, d_ff_11_q,
       d_ff_12_q, d_ff_12_qn, d_ff_13_qn, not_1_out, not_2_out, not_3_out, not_4_out, not_5_out, not_6_out,
       not_7_out, not_8_out, not_9_out, not_10_out, not_11_out, or_3_out, or_4_out, or_5_out, or_6_out,
       or_7_out, or_9_out, or_10_out, or_11_out, or_12_out, subtractor_1_bout;
  wire [2:0] multiplexer_1_out, register_1_q_2, register_2_q;
  wire [3:0] multiplexer_2_out, multiplexer_3_out, multiplexer_4_out, register_4_q, register_5_q,
       register_6_q, subtractor_2_out, subtractor_3_out, subtractor_4_out;
  wire [4:0] demultiplexer_1_out1, demultiplexer_2_out0, demultiplexer_2_out1, demultiplexer_2_out1_2,
       demultiplexer_3_out1, demultiplexer_4_out1, demultiplexer_5_out1, demultiplexer_6_out0,
       demultiplexer_7_out1, demultiplexer_11_out0, demultiplexer_12_out1, multiplexer_5_out,
       multiplexer_6_out, multiplexer_7_out, multiplexer_8_out, register_1_q_4, register_1_q_5,
       register_2_q_2, register_8_q;
  wire [4:3] register_1_q_3;
  wire [14:0] demultiplexer_9_out1, demultiplexer_13_out1;
  wire [15:0] demultiplexer_2_out0_2, demultiplexer_2_out1_3, demultiplexer_6_out0_2, demultiplexer_6_out1,
       demultiplexer_8_out0, demultiplexer_8_out1, demultiplexer_10_out0, demultiplexer_11_out0_2,
       demultiplexer_11_out1, multiplexer_9_out, multiplexer_10_out, multiplexer_11_out, multiplexer_12_out,
       multiplexer_13_out, or_8_out, register_3_q, register_7_q, register_9_q;
  wire [15:5] register_8_q_2;
  wire [15:8] register_2_q_3;
  wire [15:15] register_1_q;

  Demultiplexer #(.width(5)) demultiplexer_1 (
    .out1(demultiplexer_1_out1), .in(demultiplexer_2_out0), .sel(and_4_out));  // open: out0
  Demultiplexer #(.width(16)) demultiplexer_2 (
    .out0({demultiplexer_2_out0_2[15:10], demultiplexer_2_out0, demultiplexer_2_out0_2[4:0]}),
    .out1({demultiplexer_2_out1_3[15], demultiplexer_2_out1, demultiplexer_2_out1_2, demultiplexer_2_out1_3[4:0]}),
    .in({register_1_q[15], register_1_q_3, register_1_q_2, register_1_q_4, register_1_q_5}),
    .sel(subtractor_1_bout));
  Demultiplexer #(.width(5)) demultiplexer_3 (
    .out1(demultiplexer_3_out1), .in(demultiplexer_2_out1), .sel(and_5_out));  // open: out0
  Demultiplexer #(.width(5)) demultiplexer_4 (
    .out1(demultiplexer_4_out1), .in(demultiplexer_2_out1_2), .sel(and_4_out));  // open: out0
  not not_1 (not_1_out, CLK);
  D_Flip_Flop d_ff_1 (.D(INSTRUCTION_READY_IN), .clk(CLK), .Q(d_ff_1_q), .reset(d_ff_2_q));  // open: Qn, preset
  Demultiplexer #(.width(5)) demultiplexer_5 (
    .out1(demultiplexer_5_out1), .in(demultiplexer_8_out1[4:0]), .sel(and_6_out));  // open: out0
  D_Flip_Flop d_ff_2 (.D(RESET), .clk(CLK), .Q(d_ff_2_q), .reset(and_1_out));  // open: Qn, preset
  and and_1 (and_1_out, d_ff_2_q, not_1_out);
  Subtractor #(.width(5)) subtractor_1 (.a(register_1_q_5), .b(5'b01110), .bout(subtractor_1_bout));  // open: out, bin
  Demultiplexer #(.width(16)) demultiplexer_6 (
    .out0({demultiplexer_6_out0_2[15:6], demultiplexer_6_out0, demultiplexer_6_out0_2[0]}),
    .out1(demultiplexer_6_out1), .in(demultiplexer_8_out0), .sel(demultiplexer_8_out0[0]));
  Demultiplexer #(.width(5)) demultiplexer_7 (
    .out1(demultiplexer_7_out1), .in(demultiplexer_6_out0), .sel(and_5_out));  // open: out0
  Demultiplexer #(.width(16)) demultiplexer_8 (
    .out0(demultiplexer_8_out0), .out1(demultiplexer_8_out1),
    .in({register_2_q_3, register_2_q, register_2_q_2}), .sel(subtractor_1_bout));
  Demultiplexer #(.width(15)) demultiplexer_9 (
    .out1(demultiplexer_9_out1), .in(demultiplexer_6_out1[15:1]), .sel(and_5_out));  // open: out0
  and and_2 (and_2_out, CLK, d_ff_1_q);
  D_Flip_Flop d_ff_3 (
    .D(INSTRUCTION_READY_IN), .clk(and_3_out), .Q(d_ff_3_q), .Qn(d_ff_3_qn), .reset(d_ff_2_q));  // open: preset
  and and_3 (and_3_out, CLK, d_ff_3_qn);
  Demultiplexer #(.width(16)) demultiplexer_10 (
    .out0(demultiplexer_10_out0), .in(register_3_q), .sel(subtractor_1_bout));  // open: out1
  Demultiplexer #(.width(16)) demultiplexer_11 (
    .out0({demultiplexer_11_out0_2[15:6], demultiplexer_11_out0, demultiplexer_11_out0_2[0]}),
    .out1(demultiplexer_11_out1), .in(demultiplexer_10_out0), .sel(demultiplexer_10_out0[0]));
  Demultiplexer #(.width(5)) demultiplexer_12 (
    .out1(demultiplexer_12_out1), .in(demultiplexer_11_out0), .sel(and_6_out));  // open: out0
  D_Flip_Flop d_ff_4 (.D(1'b1), .clk(and_2_out), .Q(d_ff_4_q), .reset(d_ff_2_q));  // open: Qn, preset
  Register #(.width(16)) register_1 (
    .D(DATA_0), .en(1'b1), .clk(d_ff_4_q),
    .Q({register_1_q[15], register_1_q_3, register_1_q_2, register_1_q_4, register_1_q_5}), .clr(d_ff_2_q));
  Demultiplexer #(.width(15)) demultiplexer_13 (
    .out1(demultiplexer_13_out1), .in(demultiplexer_11_out1[15:1]), .sel(and_6_out));  // open: out0
  D_Flip_Flop d_ff_5 (.D(1'b1), .clk(and_2_out), .Q(d_ff_5_q), .reset(d_ff_2_q));  // open: Qn, preset
  Register #(.width(16)) register_2 (
    .D(DATA_1), .en(1'b1), .clk(d_ff_5_q), .Q({register_2_q_3, register_2_q, register_2_q_2}), .clr(d_ff_2_q));
  not not_2 (not_2_out, and_14_out);
  and and_4 (and_4_out, not_2_out, d_ff_7_q);
  not not_3 (not_3_out, and_19_out);
  and and_5 (and_5_out, not_3_out, d_ff_7_q, and_14_out);
  not not_4 (not_4_out, and_24_out);
  and and_6 (and_6_out, d_ff_7_q, not_4_out, and_14_out, and_19_out);
  Register #(.width(16)) register_3 (.D(DATA_2), .en(1'b1), .clk(d_ff_6_q), .Q(register_3_q), .clr(d_ff_2_q));
  D_Flip_Flop d_ff_6 (.D(1'b1), .clk(and_2_out), .Q(d_ff_6_q), .reset(d_ff_2_q));  // open: Qn, preset
  assign REG_ADRESS = demultiplexer_12_out1 | demultiplexer_7_out1 | demultiplexer_5_out1 | demultiplexer_4_out1 | demultiplexer_3_out1 | demultiplexer_1_out1;  // OR_Gate or_1, 5 bits wide
  D_Flip_Flop d_ff_7 (.D(1'b1), .clk(and_7_out), .Q(d_ff_7_q), .reset(d_ff_2_q));  // open: Qn, preset
  and and_7 (and_7_out, d_ff_3_q, CLK);
  Multiplexer #(.width(3)) multiplexer_1 (
    .in0(register_1_q_2), .in1(register_2_q), .out(multiplexer_1_out), .sel(subtractor_1_bout));
  assign RAM_ADRESS = demultiplexer_13_out1 | demultiplexer_9_out1;  // OR_Gate or_2, 15 bits wide
  not not_5 (not_5_out, multiplexer_1_out[0]);
  not not_6 (not_6_out, multiplexer_1_out[1]);
  not not_7 (not_7_out, multiplexer_1_out[2]);
  D_Flip_Flop d_ff_8 (
    .D(multiplexer_1_out[0]), .clk(CLK), .Q(d_ff_8_q), .Qn(d_ff_8_qn), .reset(d_ff_2_q));  // open: preset
  not not_8 (not_8_out, adress_comparator_4bit_1_output_adress);
  and and_8 (and_8_out, and_5_out, demultiplexer_8_out0[0]);
  and and_9 (and_9_out, and_6_out, demultiplexer_10_out0[0]);
  or or_3 (or_3_out, and_8_out, and_9_out);
  and and_10 (READ_RAM, or_3_out, not_9_out);
  and and_11 (and_11_out, d_ff_7_q, d_ff_8_qn);
  and and_12 (and_12_out, not_8_out, d_ff_7_q);
  or or_4 (or_4_out, and_12_out, and_11_out);
  not not_9 (not_9_out, subtractor_1_bout);
  Subtractor #(.width(4)) subtractor_2 (.a(register_4_q), .b(4'b0001), .out(subtractor_2_out));  // open: bin, bout
  Register #(.width(4)) register_4 (
    .D(multiplexer_2_out), .en(1'b1), .clk(and_13_out), .Q(register_4_q), .clr(d_ff_2_q));
  Multiplexer #(.width(4)) multiplexer_2 (
    .in0(subtractor_2_out), .in1(4'b0100), .out(multiplexer_2_out), .sel(d_ff_8_qn));
  and and_13 (and_13_out, or_4_out, multiplexer_1_out[0], CLK);
  and and_14 (and_14_out, d_ff_7_q, or_5_out);
  or or_5 (or_5_out, not_5_out, or_6_out);
  and and_15 (and_15_out, d_ff_7_q, not_5_out);
  and and_16 (and_16_out, d_ff_8_q, adress_comparator_4bit_1_output_adress);
  Adress_Comparator_4bit adress_comparator_4bit_1 (
    .ADRESS(register_4_q), .PHYSICAL_ADRESS(4'b0000), .OUTPUT_ADRESS(adress_comparator_4bit_1_output_adress));
  D_Flip_Flop d_ff_9 (.D(or_6_out), .clk(CLK), .Q(d_ff_9_q), .reset(d_ff_2_q));  // open: Qn, preset
  or or_6 (or_6_out, and_15_out, and_16_out);
  D_Flip_Flop d_ff_10 (
    .D(multiplexer_1_out[1]), .clk(CLK), .Q(d_ff_10_q), .Qn(d_ff_10_qn), .reset(d_ff_2_q));  // open: preset
  and and_17 (and_17_out, not_10_out, d_ff_9_q);
  or or_7 (or_7_out, and_17_out, d_ff_10_qn);
  not not_10 (not_10_out, adress_comparator_4bit_2_output_adress);
  assign or_8_out = INPUT_REG | INPUT_RAM;  // OR_Gate or_8, 16 bits wide
  Register #(.width(4)) register_5 (
    .D(multiplexer_3_out), .en(1'b1), .clk(and_18_out), .Q(register_5_q), .clr(d_ff_2_q));
  Multiplexer #(.width(4)) multiplexer_3 (
    .in0(subtractor_3_out), .in1(4'b0100), .out(multiplexer_3_out), .sel(d_ff_10_qn));
  and and_18 (and_18_out, or_7_out, multiplexer_1_out[1], CLK);
  Subtractor #(.width(4)) subtractor_3 (.a(register_5_q), .b(4'b0001), .out(subtractor_3_out));  // open: bin, bout
  and and_19 (and_19_out, d_ff_7_q, or_9_out);
  or or_9 (or_9_out, not_6_out, or_10_out);
  and and_20 (and_20_out, d_ff_9_q, not_6_out);
  D_Flip_Flop d_ff_11 (.D(or_10_out), .clk(CLK), .Q(d_ff_11_q), .reset(d_ff_2_q));  // open: Qn, preset
  and and_21 (and_21_out, d_ff_10_q, adress_comparator_4bit_2_output_adress);
  or or_10 (or_10_out, and_20_out, and_21_out);
  Adress_Comparator_4bit adress_comparator_4bit_2 (
    .ADRESS(register_5_q), .PHYSICAL_ADRESS(4'b0000), .OUTPUT_ADRESS(adress_comparator_4bit_2_output_adress));
  D_Flip_Flop d_ff_12 (
    .D(multiplexer_1_out[2]), .clk(CLK), .Q(d_ff_12_q), .Qn(d_ff_12_qn), .reset(d_ff_2_q));  // open: preset
  and and_22 (and_22_out, not_11_out, d_ff_11_q);
  not not_11 (not_11_out, adress_comparator_4bit_3_output_adress);
  or or_11 (or_11_out, and_22_out, d_ff_12_qn);
  Subtractor #(.width(4)) subtractor_4 (.a(register_6_q), .b(4'b0001), .out(subtractor_4_out));  // open: bin, bout
  Register #(.width(4)) register_6 (
    .D(multiplexer_4_out), .en(1'b1), .clk(and_23_out), .Q(register_6_q), .clr(d_ff_2_q));
  Multiplexer #(.width(4)) multiplexer_4 (
    .in0(subtractor_4_out), .in1(4'b0100), .out(multiplexer_4_out), .sel(d_ff_12_qn));
  and and_23 (and_23_out, or_11_out, multiplexer_1_out[2], CLK);
  and and_24 (and_24_out, d_ff_7_q, or_12_out);
  or or_12 (or_12_out, not_7_out, and_25_out);
  and and_25 (and_25_out, d_ff_12_q, adress_comparator_4bit_3_output_adress);
  Adress_Comparator_4bit adress_comparator_4bit_3 (
    .ADRESS(register_6_q), .PHYSICAL_ADRESS(4'b0000), .OUTPUT_ADRESS(adress_comparator_4bit_3_output_adress));
  and and_26 (and_26_out, and_14_out, and_19_out, and_24_out);
  Register #(.width(16)) register_7 (.D(or_8_out), .en(1'b1), .clk(and_14_out), .Q(register_7_q));  // open: clr
  Register #(.width(16)) register_8 (
    .D(or_8_out), .en(1'b1), .clk(and_19_out), .Q({register_8_q_2, register_8_q}));  // open: clr
  Register #(.width(16)) register_9 (.D(or_8_out), .en(1'b1), .clk(and_24_out), .Q(register_9_q));  // open: clr
  Multiplexer #(.width(5)) multiplexer_5 (
    .in0(register_1_q_4), .in1(register_7_q[4:0]), .out(multiplexer_5_out), .sel(register_2_q[0]));
  Multiplexer #(.width(5)) multiplexer_6 (
    .in0({register_1_q_3, register_1_q_2}), .in1(register_8_q), .out(multiplexer_6_out), .sel(register_2_q[1]));
  Multiplexer #(.width(5)) multiplexer_7 (
    .in0(register_2_q_2), .in1(register_9_q[4:0]), .out(multiplexer_7_out), .sel(register_2_q[2]));
  Multiplexer #(.width(5)) multiplexer_8 (
    .in0(register_1_q_4), .in1(register_7_q[4:0]), .out(multiplexer_8_out), .sel(register_1_q_2[0]));
  Multiplexer #(.width(16)) multiplexer_9 (
    .in0({register_2_q_3, register_2_q, register_2_q_2}), .in1({register_8_q_2, register_8_q}),
    .out(multiplexer_9_out), .sel(register_1_q_2[1]));
  Multiplexer #(.width(16)) multiplexer_10 (
    .in0(register_3_q), .in1(register_9_q), .out(multiplexer_10_out), .sel(register_1_q_2[2]));
  D_Flip_Flop d_ff_13 (.D(and_26_out), .clk(CLK), .Qn(d_ff_13_qn), .reset(d_ff_2_q));  // open: Q, preset
  and and_27 (INSTRUCTION_READY_OUT, and_26_out, d_ff_13_qn);
  Multiplexer #(.width(16)) multiplexer_11 (
    .in0({{6{1'b0}}, multiplexer_8_out, register_1_q_5}),
    .in1({1'b0, multiplexer_6_out, multiplexer_5_out, register_1_q_5}), .out(multiplexer_11_out),
    .sel(subtractor_1_bout));
  Multiplexer #(.width(16)) multiplexer_12 (
    .in0(multiplexer_9_out), .in1({{11{1'b0}}, multiplexer_7_out}), .out(multiplexer_12_out),
    .sel(subtractor_1_bout));
  Multiplexer #(.width(16)) multiplexer_13 (
    .in0(multiplexer_10_out), .in1({16{1'b0}}), .out(multiplexer_13_out), .sel(subtractor_1_bout));
  Multiplexer #(.width(16)) multiplexer_14 (
    .in0({16{1'b0}}), .in1(multiplexer_11_out), .out(OUTPUT_0), .sel(and_26_out));
  Multiplexer #(.width(16)) multiplexer_15 (
    .in0({16{1'b0}}), .in1(multiplexer_12_out), .out(OUTPUT_1), .sel(and_26_out));
  Multiplexer #(.width(16)) multiplexer_16 (
    .in0({16{1'b0}}), .in1(multiplexer_13_out), .out(OUTPUT_2), .sel(and_26_out));
endmodule
