// Logisim project Inputs.circ as structural Verilog: 1 circuit, main circuit Inputs
module Inputs (
  input  [3:0] ADRESS,
  input  CLK,
  input  [15:0] INPUT_1,
  input  [15:0] INPUT_2,
  input  [15:0] INPUT_3,
  input  [15:0] INPUT_4,
  input  [15:0] INPUT_5,
  input  [15:0] INPUT_6,
  input  [15:0] INPUT_7,
  input  [15:0] INPUT_8,
  input  [15:0] INPUT_9,
  input  [15:0] INPUT_10,
  input  [15:0] INPUT_11,
  input  [15:0] INPUT_12,
  input  [15:0] INPUT_13,
  input  [15:0] INPUT_14,
  input  [15:0] INPUT_15,
  output [15:0] DATA_OUT
);

  wire [3:0] register_1_q;

  Register #(.width(4)) register_1 (.D(ADRESS), .en(1'b1), .clk(CLK), .Q(register_1_q));  // open: clr
  Multiplexer #(.select(4), .width(16)) multiplexer_1 (
    .in0({16{1'b0}}), .in1(INPUT_1), .in2(INPUT_2), .in3(INPUT_3), .in4(INPUT_4), .in5(INPUT_5),
    .in6(INPUT_6), .in7(INPUT_7), .in8(INPUT_8), .in9(INPUT_9), .in10(INPUT_10), .in11(INPUT_11),
    .in12(INPUT_12), .in13(INPUT_13), .in14(INPUT_14), .in15(INPUT_15), .out(DATA_OUT), .sel(register_1_q));
endmodule
