// Logisim project Instruction_Fetch_Buffer.circ as structural Verilog: 1 circuit, main circuit Instruction_Fetch_Buffer
module Instruction_Fetch_Buffer (
  input  [15:0] DATA_IN,
  input  CLK,
  input  RESET,
  input  OUTPUT_ON_FULL,
  output [4:0] OPCODE,
  output [15:0] OUTPUT_0,
  output [15:0] OUTPUT_1,
  output [15:0] OUTPUT_2,
  output FETCH,
  output EMPTY,
  output INSTRUCTION_READY
);

  wire adress_comparator_5bit_1_output_adress, adress_comparator_5bit_2_output_adress,
       adress_comparator_5bit_3_output_adress, adress_comparator_5bit_4_output_adress,
       adress_comparator_5bit_5_output_adress, adress_comparator_5bit_6_output_adress, and_1_out, and_2_out,
       and_3_out, and_4_out, and_5_out, d_ff_1_q, d_ff_2_q, d_ff_3_q, d_ff_4_q, d_ff_5_qn, not_1_out,
       not_2_out, not_3_out, not_4_out, not_5_out, not_6_out, not_7_out, not_8_out, not_9_out, not_10_out,
       not_11_out, not_12_out, not_13_out, or_1_out, or_2_out, or_3_out, or_4_out, or_5_out, or_6_out,
       or_8_out;
  wire [4:0] multiplexer_1_out;
  wire [15:0] multiplexer_2_out, multiplexer_4_out, multiplexer_6_out, register_2_q, register_3_q;
  wire [15:5] register_1_q;

  Adress_Comparator_5bit adress_comparator_5bit_1 (
    .ADRESS(multiplexer_1_out), .PHYSICAL_ADRESS(5'b00011),
    .OUTPUT_ADRESS(adress_comparator_5bit_1_output_adress));
  Adress_Comparator_5bit adress_comparator_5bit_2 (
    .ADRESS(multiplexer_1_out), .PHYSICAL_ADRESS(5'b00100),
    .OUTPUT_ADRESS(adress_comparator_5bit_2_output_adress));
  Adress_Comparator_5bit adress_comparator_5bit_3 (
    .ADRESS(multiplexer_1_out), .PHYSICAL_ADRESS(5'b01000),
    .OUTPUT_ADRESS(adress_comparator_5bit_3_output_adress));
  Adress_Comparator_5bit adress_comparator_5bit_4 (
    .ADRESS(multiplexer_1_out), .PHYSICAL_ADRESS(5'b10110),
    .OUTPUT_ADRESS(adress_comparator_5bit_4_output_adress));
  or or_1 (or_1_out, adress_comparator_5bit_1_output_adress, or_2_out);
  or or_2 (or_2_out, adress_comparator_5bit_2_output_adress, adress_comparator_5bit_3_output_adress);
  or or_3 (or_3_out, or_1_out, adress_comparator_5bit_4_output_adress);
  Adress_Comparator_5bit adress_comparator_5bit_5 (
    .ADRESS(multiplexer_1_out), .PHYSICAL_ADRESS(5'b01111),
    .OUTPUT_ADRESS(adress_comparator_5bit_5_output_adress));
  or or_4 (or_4_out, adress_comparator_5bit_5_output_adress, adress_comparator_5bit_6_output_adress);
  Adress_Comparator_5bit adress_comparator_5bit_6 (
    .ADRESS(multiplexer_1_out), .PHYSICAL_ADRESS(5'b10100),
    .OUTPUT_ADRESS(adress_comparator_5bit_6_output_adress));
  D_Flip_Flop d_ff_1 (.D(RESET), .clk(CLK), .Q(d_ff_1_q), .reset(d_ff_1_q));  // open: Qn, preset
  not not_1 (not_1_out, or_4_out);
  D_Flip_Flop d_ff_2 (.D(1'b1), .clk(CLK), .Q(d_ff_2_q), .reset(d_ff_1_q));  // open: Qn, preset
  D_Flip_Flop d_ff_3 (.D(d_ff_2_q), .clk(CLK), .Q(d_ff_3_q), .reset(or_5_out));  // open: Qn, preset
  or or_5 (or_5_out, d_ff_1_q, or_3_out);
  D_Flip_Flop d_ff_4 (.D(d_ff_3_q), .clk(CLK), .Q(d_ff_4_q), .reset(or_6_out));  // open: Qn, preset
  or or_6 (or_6_out, d_ff_1_q, not_1_out, or_3_out);
  Multiplexer #(.width(5)) multiplexer_1 (.in0(DATA_IN[4:0]), .in1(OPCODE), .out(multiplexer_1_out), .sel(d_ff_2_q));
  not not_2 (not_2_out, d_ff_2_q);
  not not_3 (not_3_out, or_3_out);
  and and_1 (and_1_out, not_2_out, not_3_out, not_4_out);
  not not_4 (not_4_out, or_4_out);
  not not_5 (not_5_out, d_ff_3_q);
  not not_6 (not_6_out, or_3_out);
  and and_2 (and_2_out, not_5_out, not_6_out, or_4_out);
  not not_7 (not_7_out, or_3_out);
  not not_8 (not_8_out, or_4_out);
  and and_3 (and_3_out, not_7_out, not_8_out, d_ff_3_q);
  not not_9 (not_9_out, or_4_out);
  and and_4 (and_4_out, or_3_out, not_9_out, d_ff_2_q);
  not not_10 (not_10_out, or_3_out);
  and and_5 (and_5_out, not_10_out, or_4_out, d_ff_4_q);
  or or_7 (FETCH, and_1_out, and_2_out);
  or or_8 (or_8_out, and_3_out, and_4_out, and_5_out);
  Register #(.width(16)) register_1 (
    .D(DATA_IN), .en(1'b1), .clk(d_ff_2_q), .Q({register_1_q, OPCODE}), .clr(d_ff_1_q));
  Register #(.width(16)) register_2 (.D(DATA_IN), .en(1'b1), .clk(d_ff_3_q), .Q(register_2_q), .clr(or_5_out));
  Register #(.width(16)) register_3 (.D(DATA_IN), .en(1'b1), .clk(d_ff_4_q), .Q(register_3_q), .clr(or_6_out));
  not not_11 (not_11_out, d_ff_4_q);
  not not_12 (not_12_out, d_ff_3_q);
  not not_13 (not_13_out, d_ff_2_q);
  and and_6 (EMPTY, not_11_out, not_12_out, not_13_out);
  Multiplexer #(.width(16)) multiplexer_2 (
    .in0({16{1'b0}}), .in1({register_1_q, OPCODE}), .out(multiplexer_2_out), .sel(or_8_out));
  Multiplexer #(.width(16)) multiplexer_3 (
    .in0({register_1_q, OPCODE}), .in1(multiplexer_2_out), .out(OUTPUT_0), .sel(OUTPUT_ON_FULL));
  Multiplexer #(.width(16)) multiplexer_4 (
    .in0({16{1'b0}}), .in1(register_2_q), .out(multiplexer_4_out), .sel(or_8_out));
  Multiplexer #(.width(16)) multiplexer_5 (
    .in0(register_2_q), .in1(multiplexer_4_out), .out(OUTPUT_1), .sel(OUTPUT_ON_FULL));
  Multiplexer #(.width(16)) multiplexer_6 (
    .in0({16{1'b0}}), .in1(register_3_q), .out(multiplexer_6_out), .sel(or_8_out));
  Multiplexer #(.width(16)) multiplexer_7 (
    .in0(register_3_q), .in1(multiplexer_6_out), .out(OUTPUT_2), .sel(OUTPUT_ON_FULL));
  D_Flip_Flop d_ff_5 (.D(or_8_out), .clk(CLK), .Qn(d_ff_5_qn), .reset(d_ff_1_q));  // open: Q, preset
  and and_7 (INSTRUCTION_READY, or_8_out, d_ff_5_qn);
endmodule
