// Logisim project Kronos v2.circ as structural Verilog: 1 circuit, main circuit main
module main (
  input  in_1,
  input  RESET
);

  wire and_1_out, and_2_out, and_3_out, and_4_out, and_5_out, and_6_out, button_1_out, button_2_out,
       button_3_out, CLK_out, clock_1_out, clock_kronos_1_clock_out, cycle_counter_1_instruction_end,
       cycle_counter_1_instruction_state_2, d_ff_1_q, demultiplexer_1_out0, demultiplexer_1_out1,
       demultiplexer_11_out1, demultiplexer_11_out2, demultiplexer_11_out3, demultiplexer_11_out4,
       demultiplexer_11_out5, demultiplexer_11_out6, demultiplexer_11_out7, demultiplexer_11_out8,
       demultiplexer_11_out9, demultiplexer_11_out10, demultiplexer_11_out11, demultiplexer_11_out12,
       demultiplexer_11_out13, demultiplexer_11_out14, demultiplexer_11_out15, demultiplexer_11_out16,
       demultiplexer_11_out17, demultiplexer_11_out18, demultiplexer_11_out19, demultiplexer_11_out20,
       demultiplexer_11_out21, demultiplexer_11_out22, demultiplexer_11_out23, demultiplexer_12_out0,
       demultiplexer_12_out1, dipswitch_1_p1, dipswitch_1_p2,
       indirect_adressing_unit_1_instruction_ready_out, indirect_adressing_unit_1_read_ram,
       instruction_fetch_buffer_1_empty, instruction_fetch_buffer_1_fetch,
       instruction_fetch_buffer_1_instruction_ready, multiplexer_1_out, multiplexer_4_out, not_1_out,
       or_1_out, or_2_out, or_4_out, or_5_out, or_8_out, or_10_out, or_11_out, or_22_out, or_24_out,
       or_28_out, or_30_out, or_31_out;
  wire [0:0] or_23_out, or_26_out_2;
  wire [3:0] or_27_out, undriven;
  wire [4:0] demultiplexer_4_out0, indirect_adressing_unit_1_output_0, indirect_adressing_unit_1_reg_adress,
       multiplexer_5_out, or_7_out, or_9_out, or_12_out, or_13_out, or_21_out;
  wire [14:0] demultiplexer_4_out1, demultiplexer_6_out0, demultiplexer_6_out1, demultiplexer_7_out0,
       demultiplexer_7_out1, demultiplexer_10_out0, demultiplexer_10_out1,
       indirect_adressing_unit_1_ram_adress, multiplexer_3_out, or_15_out, or_23_out_2, or_26_out;
  wire [14:5] demultiplexer_4_out0_2;
  wire [15:0] alu_1_data_out, demultiplexer_2_out1, demultiplexer_2_out2, demultiplexer_2_out3,
       demultiplexer_2_out4, demultiplexer_2_out5, demultiplexer_2_out6, demultiplexer_2_out7,
       demultiplexer_2_out8, demultiplexer_2_out9, demultiplexer_2_out10, demultiplexer_2_out11,
       demultiplexer_2_out12, demultiplexer_2_out13, demultiplexer_2_out14, demultiplexer_2_out16,
       demultiplexer_2_out18, demultiplexer_2_out19, demultiplexer_3_out0, demultiplexer_3_out1,
       demultiplexer_5_out1, demultiplexer_5_out2, demultiplexer_5_out5, demultiplexer_5_out6,
       demultiplexer_5_out7, demultiplexer_5_out9, demultiplexer_5_out10, demultiplexer_5_out11,
       demultiplexer_5_out12, demultiplexer_5_out13, demultiplexer_5_out14, demultiplexer_5_out15,
       demultiplexer_5_out16, demultiplexer_5_out17, demultiplexer_5_out18, demultiplexer_5_out19,
       demultiplexer_5_out20, demultiplexer_5_out21, demultiplexer_5_out23, demultiplexer_8_out15,
       demultiplexer_8_out20, demultiplexer_9_out0, demultiplexer_9_out1, dipswitch_2_sw16, dipswitch_3_sw16,
       dipswitch_4_sw16, dipswitch_5_sw16, dipswitch_6_sw16, dipswitch_7_sw16, dipswitch_8_sw16,
       dipswitch_9_sw16, dipswitch_10_sw16, dipswitch_11_sw16, dipswitch_12_sw16, dipswitch_13_sw16,
       dipswitch_14_sw16, dipswitch_15_sw16, dipswitch_16_sw16, indirect_adressing_unit_1_output_1,
       indirect_adressing_unit_1_output_2, inputs_1_data_out, instruction_fetch_buffer_1_output_0,
       instruction_fetch_buffer_1_output_1, instruction_fetch_buffer_1_output_2, multiplexer_2_out, or_3_out,
       or_6_out, or_14_out, or_16_out, or_17_out, or_18_out, or_19_out, or_20_out, or_25_out, or_29_out,
       outputs_1_output_1, outputs_1_output_2, outputs_1_output_3, outputs_1_output_4, outputs_1_output_5,
       outputs_1_output_6, outputs_1_output_7, outputs_1_output_8, outputs_1_output_9, outputs_1_output_10,
       outputs_1_output_11, outputs_1_output_12, outputs_1_output_13, outputs_1_output_14,
       outputs_1_output_15, program_counter_1_out_6, ram_1_dout, register_1_q, register_type32_1_data_0,
       register_type32_1_data_1, rom_1_data, stack_1_output_stack, undriven_2;
  wire [15:5] indirect_adressing_unit_1_output_0_2, or_21_out_2;

  Button CLK (.out(CLK_out));
  RAM #(.addrWidth(15), .dataWidth(16), .enables("line")) ram_1 (
    .addr(or_15_out), .we(or_22_out), .clk(clock_kronos_1_clock_out), .din(or_20_out), .dout(ram_1_dout));
  Clock clock_1 (.out(clock_1_out));
  // DipSwitch #(.number(2)) dipswitch_1: pin names not known; wires that end beside it: dipswitch_1_p1, dipswitch_1_p2
  or or_1 (or_1_out, CLK_out, in_1);
  ROM #(.addrWidth(16), .dataWidth(16)) rom_1 (.addr(program_counter_1_out_6), .data(rom_1_data));
  Multiplexer multiplexer_1 (
    .in0(1'b0), .in1(alu_1_data_out[0]), .out(multiplexer_1_out), .sel(demultiplexer_11_out16));
  and and_1 (and_1_out, clock_kronos_1_clock_out, or_2_out);
  or or_2 (or_2_out, instruction_fetch_buffer_1_empty, RESET);
  assign or_3_out = multiplexer_2_out | register_type32_1_data_0;  // OR_Gate or_3, 16 bits wide
  Multiplexer #(.width(16)) multiplexer_2 (
    .in0({16{1'b0}}), .in1(ram_1_dout), .out(multiplexer_2_out), .sel(or_28_out));
  Clock_Kronos clock_kronos_1 (
    .CLOCK_FREQUENCY(clock_1_out), .CLOCK_ON(dipswitch_1_p1), .MANUAL(or_1_out), .HALT(dipswitch_1_p2),
    .CLOCK_OUT(clock_kronos_1_clock_out));
  Register_Type32 register_type32_1 (
    .CLK(clock_kronos_1_clock_out), .WRITE(or_30_out), .DATA_IN(or_19_out), .WRITE_ADRESS(or_13_out),
    .READ_0(or_9_out), .READ_1(or_7_out), .DATA_0(register_type32_1_data_0), .DATA_1(register_type32_1_data_1));
  ALU alu_1 (
    .OPCODE(or_12_out), .OPERAND_1(register_type32_1_data_0), .OPERAND_2(register_type32_1_data_1),
    .DATA_OUT(alu_1_data_out));
  or or_4 (or_4_out, button_1_out, RESET, cycle_counter_1_instruction_end);
  Button button_1 (.out(button_1_out));
  and and_2 (and_2_out, not_1_out, or_8_out);
  and and_3 (and_3_out, or_24_out, cycle_counter_1_instruction_state_2);
  not not_1 (not_1_out, and_3_out);
  or or_5 (or_5_out, RESET, button_2_out);
  Button button_2 (.out(button_2_out));
  Register #(.width(16)) register_1 (.D(or_6_out), .en(1'b1), .clk(d_ff_1_q), .Q(register_1_q), .clr(and_1_out));
  assign or_6_out = register_type32_1_data_0 | multiplexer_2_out;  // OR_Gate or_6, 16 bits wide
  D_Flip_Flop d_ff_1 (
    .D(cycle_counter_1_instruction_state_2), .clk(and_4_out), .Q(d_ff_1_q), .reset(and_1_out));  // open: Qn, preset
  and and_4 (and_4_out, demultiplexer_11_out20, clock_kronos_1_clock_out);
  assign or_7_out = or_14_out[14:10];  // OR_Gate or_7, 5 bits wide OR_Gate
  or or_8 (or_8_out, instruction_fetch_buffer_1_fetch, cycle_counter_1_instruction_end);
  Outputs outputs_1 (
    .RESET(RESET), .WRITE(demultiplexer_11_out18), .OUTPUT_ADRESS(or_27_out), .DATA_IN(or_3_out),
    .CLK(clock_kronos_1_clock_out), .OUTPUT_1(outputs_1_output_1), .OUTPUT_2(outputs_1_output_2),
    .OUTPUT_3(outputs_1_output_3), .OUTPUT_4(outputs_1_output_4), .OUTPUT_5(outputs_1_output_5),
    .OUTPUT_6(outputs_1_output_6), .OUTPUT_7(outputs_1_output_7), .OUTPUT_8(outputs_1_output_8),
    .OUTPUT_9(outputs_1_output_9), .OUTPUT_10(outputs_1_output_10), .OUTPUT_11(outputs_1_output_11),
    .OUTPUT_12(outputs_1_output_12), .OUTPUT_13(outputs_1_output_13), .OUTPUT_14(outputs_1_output_14),
    .OUTPUT_15(outputs_1_output_15));
  Instruction_Fetch_Buffer instruction_fetch_buffer_1 (
    .DATA_IN(rom_1_data), .CLK(clock_kronos_1_clock_out), .RESET(or_4_out), .OUTPUT_ON_FULL(1'b1),
    .OUTPUT_0(instruction_fetch_buffer_1_output_0), .OUTPUT_1(instruction_fetch_buffer_1_output_1),
    .OUTPUT_2(instruction_fetch_buffer_1_output_2), .FETCH(instruction_fetch_buffer_1_fetch),
    .EMPTY(instruction_fetch_buffer_1_empty), .INSTRUCTION_READY(instruction_fetch_buffer_1_instruction_ready));  // open: OPCODE
  Program_Counter program_counter_1 (
    .ADRESS(or_18_out), .NEXT_INSTRUCTION(and_2_out), .JUMP(and_3_out), .CLK(clock_kronos_1_clock_out),
    .RESET(or_5_out), .out_6(program_counter_1_out_6));
  Multiplexer #(.width(15)) multiplexer_3 (
    .in0(demultiplexer_7_out1), .in1(demultiplexer_10_out1), .out(multiplexer_3_out), .sel(d_ff_1_q));
  Multiplexer multiplexer_4 (.in0(demultiplexer_5_out20[0]), .in1(1'b0), .out(multiplexer_4_out), .sel(d_ff_1_q));
  Demultiplexer demultiplexer_1 (
    .out0(demultiplexer_1_out0), .out1(demultiplexer_1_out1), .in(d_ff_1_q), .sel(demultiplexer_8_out20[0]));
  assign or_9_out = indirect_adressing_unit_1_reg_adress | demultiplexer_7_out0[4:0] | demultiplexer_6_out0[4:0] | or_14_out[9:5] | or_16_out[9:5] | or_17_out[9:5];  // OR_Gate or_9, 5 bits wide
  LedBar #(.matrixcols(16)) ledbar_1 (
    .led0(outputs_1_output_1[15]), .led1(outputs_1_output_1[14]), .led2(outputs_1_output_1[13]),
    .led3(outputs_1_output_1[12]), .led4(outputs_1_output_1[11]), .led5(outputs_1_output_1[10]),
    .led6(outputs_1_output_1[9]), .led7(outputs_1_output_1[8]), .led8(outputs_1_output_1[7]),
    .led9(outputs_1_output_1[6]), .led10(outputs_1_output_1[5]), .led11(outputs_1_output_1[4]),
    .led12(outputs_1_output_1[3]), .led13(outputs_1_output_1[2]), .led14(outputs_1_output_1[1]),
    .led15(outputs_1_output_1[0]));
  LedBar #(.matrixcols(16)) ledbar_2 (
    .led0(outputs_1_output_2[15]), .led1(outputs_1_output_2[14]), .led2(outputs_1_output_2[13]),
    .led3(outputs_1_output_2[12]), .led4(outputs_1_output_2[11]), .led5(outputs_1_output_2[10]),
    .led6(outputs_1_output_2[9]), .led7(outputs_1_output_2[8]), .led8(outputs_1_output_2[7]),
    .led9(outputs_1_output_2[6]), .led10(outputs_1_output_2[5]), .led11(outputs_1_output_2[4]),
    .led12(outputs_1_output_2[3]), .led13(outputs_1_output_2[2]), .led14(outputs_1_output_2[1]),
    .led15(outputs_1_output_2[0]));
  LedBar #(.matrixcols(16)) ledbar_3 (
    .led0(outputs_1_output_3[15]), .led1(outputs_1_output_3[14]), .led2(outputs_1_output_3[13]),
    .led3(outputs_1_output_3[12]), .led4(outputs_1_output_3[11]), .led5(outputs_1_output_3[10]),
    .led6(outputs_1_output_3[9]), .led7(outputs_1_output_3[8]), .led8(outputs_1_output_3[7]),
    .led9(outputs_1_output_3[6]), .led10(outputs_1_output_3[5]), .led11(outputs_1_output_3[4]),
    .led12(outputs_1_output_3[3]), .led13(outputs_1_output_3[2]), .led14(outputs_1_output_3[1]),
    .led15(outputs_1_output_3[0]));
  LedBar #(.matrixcols(16)) ledbar_4 (
    .led0(outputs_1_output_4[15]), .led1(outputs_1_output_4[14]), .led2(outputs_1_output_4[13]),
    .led3(outputs_1_output_4[12]), .led4(outputs_1_output_4[11]), .led5(outputs_1_output_4[10]),
    .led6(outputs_1_output_4[9]), .led7(outputs_1_output_4[8]), .led8(outputs_1_output_4[7]),
    .led9(outputs_1_output_4[6]), .led10(outputs_1_output_4[5]), .led11(outputs_1_output_4[4]),
    .led12(outputs_1_output_4[3]), .led13(outputs_1_output_4[2]), .led14(outputs_1_output_4[1]),
    .led15(outputs_1_output_4[0]));
  LedBar #(.matrixcols(16)) ledbar_5 (
    .led0(outputs_1_output_5[15]), .led1(outputs_1_output_5[14]), .led2(outputs_1_output_5[13]),
    .led3(outputs_1_output_5[12]), .led4(outputs_1_output_5[11]), .led5(outputs_1_output_5[10]),
    .led6(outputs_1_output_5[9]), .led7(outputs_1_output_5[8]), .led8(outputs_1_output_5[7]),
    .led9(outputs_1_output_5[6]), .led10(outputs_1_output_5[5]), .led11(outputs_1_output_5[4]),
    .led12(outputs_1_output_5[3]), .led13(outputs_1_output_5[2]), .led14(outputs_1_output_5[1]),
    .led15(outputs_1_output_5[0]));
  LedBar #(.matrixcols(16)) ledbar_6 (
    .led0(outputs_1_output_6[15]), .led1(outputs_1_output_6[14]), .led2(outputs_1_output_6[13]),
    .led3(outputs_1_output_6[12]), .led4(outputs_1_output_6[11]), .led5(outputs_1_output_6[10]),
    .led6(outputs_1_output_6[9]), .led7(outputs_1_output_6[8]), .led8(outputs_1_output_6[7]),
    .led9(outputs_1_output_6[6]), .led10(outputs_1_output_6[5]), .led11(outputs_1_output_6[4]),
    .led12(outputs_1_output_6[3]), .led13(outputs_1_output_6[2]), .led14(outputs_1_output_6[1]),
    .led15(outputs_1_output_6[0]));
  LedBar #(.matrixcols(16)) ledbar_7 (
    .led0(outputs_1_output_7[15]), .led1(outputs_1_output_7[14]), .led2(outputs_1_output_7[13]),
    .led3(outputs_1_output_7[12]), .led4(outputs_1_output_7[11]), .led5(outputs_1_output_7[10]),
    .led6(outputs_1_output_7[9]), .led7(outputs_1_output_7[8]), .led8(outputs_1_output_7[7]),
    .led9(outputs_1_output_7[6]), .led10(outputs_1_output_7[5]), .led11(outputs_1_output_7[4]),
    .led12(outputs_1_output_7[3]), .led13(outputs_1_output_7[2]), .led14(outputs_1_output_7[1]),
    .led15(outputs_1_output_7[0]));
  LedBar #(.matrixcols(16)) ledbar_8 (
    .led0(outputs_1_output_8[15]), .led1(outputs_1_output_8[14]), .led2(outputs_1_output_8[13]),
    .led3(outputs_1_output_8[12]), .led4(outputs_1_output_8[11]), .led5(outputs_1_output_8[10]),
    .led6(outputs_1_output_8[9]), .led7(outputs_1_output_8[8]), .led8(outputs_1_output_8[7]),
    .led9(outputs_1_output_8[6]), .led10(outputs_1_output_8[5]), .led11(outputs_1_output_8[4]),
    .led12(outputs_1_output_8[3]), .led13(outputs_1_output_8[2]), .led14(outputs_1_output_8[1]),
    .led15(outputs_1_output_8[0]));
  LedBar #(.matrixcols(16)) ledbar_9 (
    .led0(outputs_1_output_9[15]), .led1(outputs_1_output_9[14]), .led2(outputs_1_output_9[13]),
    .led3(outputs_1_output_9[12]), .led4(outputs_1_output_9[11]), .led5(outputs_1_output_9[10]),
    .led6(outputs_1_output_9[9]), .led7(outputs_1_output_9[8]), .led8(outputs_1_output_9[7]),
    .led9(outputs_1_output_9[6]), .led10(outputs_1_output_9[5]), .led11(outputs_1_output_9[4]),
    .led12(outputs_1_output_9[3]), .led13(outputs_1_output_9[2]), .led14(outputs_1_output_9[1]),
    .led15(outputs_1_output_9[0]));
  LedBar #(.matrixcols(16)) ledbar_10 (
    .led0(outputs_1_output_10[15]), .led1(outputs_1_output_10[14]), .led2(outputs_1_output_10[13]),
    .led3(outputs_1_output_10[12]), .led4(outputs_1_output_10[11]), .led5(outputs_1_output_10[10]),
    .led6(outputs_1_output_10[9]), .led7(outputs_1_output_10[8]), .led8(outputs_1_output_10[7]),
    .led9(outputs_1_output_10[6]), .led10(outputs_1_output_10[5]), .led11(outputs_1_output_10[4]),
    .led12(outputs_1_output_10[3]), .led13(outputs_1_output_10[2]), .led14(outputs_1_output_10[1]),
    .led15(outputs_1_output_10[0]));
  LedBar #(.matrixcols(16)) ledbar_11 (
    .led0(outputs_1_output_11[15]), .led1(outputs_1_output_11[14]), .led2(outputs_1_output_11[13]),
    .led3(outputs_1_output_11[12]), .led4(outputs_1_output_11[11]), .led5(outputs_1_output_11[10]),
    .led6(outputs_1_output_11[9]), .led7(outputs_1_output_11[8]), .led8(outputs_1_output_11[7]),
    .led9(outputs_1_output_11[6]), .led10(outputs_1_output_11[5]), .led11(outputs_1_output_11[4]),
    .led12(outputs_1_output_11[3]), .led13(outputs_1_output_11[2]), .led14(outputs_1_output_11[1]),
    .led15(outputs_1_output_11[0]));
  LedBar #(.matrixcols(16)) ledbar_12 (
    .led0(outputs_1_output_12[15]), .led1(outputs_1_output_12[14]), .led2(outputs_1_output_12[13]),
    .led3(outputs_1_output_12[12]), .led4(outputs_1_output_12[11]), .led5(outputs_1_output_12[10]),
    .led6(outputs_1_output_12[9]), .led7(outputs_1_output_12[8]), .led8(outputs_1_output_12[7]),
    .led9(outputs_1_output_12[6]), .led10(outputs_1_output_12[5]), .led11(outputs_1_output_12[4]),
    .led12(outputs_1_output_12[3]), .led13(outputs_1_output_12[2]), .led14(outputs_1_output_12[1]),
    .led15(outputs_1_output_12[0]));
  LedBar #(.matrixcols(16)) ledbar_13 (
    .led0(outputs_1_output_13[15]), .led1(outputs_1_output_13[14]), .led2(outputs_1_output_13[13]),
    .led3(outputs_1_output_13[12]), .led4(outputs_1_output_13[11]), .led5(outputs_1_output_13[10]),
    .led6(outputs_1_output_13[9]), .led7(outputs_1_output_13[8]), .led8(outputs_1_output_13[7]),
    .led9(outputs_1_output_13[6]), .led10(outputs_1_output_13[5]), .led11(outputs_1_output_13[4]),
    .led12(outputs_1_output_13[3]), .led13(outputs_1_output_13[2]), .led14(outputs_1_output_13[1]),
    .led15(outputs_1_output_13[0]));
  LedBar #(.matrixcols(16)) ledbar_14 (
    .led0(outputs_1_output_14[15]), .led1(outputs_1_output_14[14]), .led2(outputs_1_output_14[13]),
    .led3(outputs_1_output_14[12]), .led4(outputs_1_output_14[11]), .led5(outputs_1_output_14[10]),
    .led6(outputs_1_output_14[9]), .led7(outputs_1_output_14[8]), .led8(outputs_1_output_14[7]),
    .led9(outputs_1_output_14[6]), .led10(outputs_1_output_14[5]), .led11(outputs_1_output_14[4]),
    .led12(outputs_1_output_14[3]), .led13(outputs_1_output_14[2]), .led14(outputs_1_output_14[1]),
    .led15(outputs_1_output_14[0]));
  LedBar #(.matrixcols(16)) ledbar_15 (
    .led0(outputs_1_output_15[15]), .led1(outputs_1_output_15[14]), .led2(outputs_1_output_15[13]),
    .led3(outputs_1_output_15[12]), .led4(outputs_1_output_15[11]), .led5(outputs_1_output_15[10]),
    .led6(outputs_1_output_15[9]), .led7(outputs_1_output_15[8]), .led8(outputs_1_output_15[7]),
    .led9(outputs_1_output_15[6]), .led10(outputs_1_output_15[5]), .led11(outputs_1_output_15[4]),
    .led12(outputs_1_output_15[3]), .led13(outputs_1_output_15[2]), .led14(outputs_1_output_15[1]),
    .led15(outputs_1_output_15[0]));
  or or_10 (or_10_out, instruction_fetch_buffer_1_empty, button_3_out);
  or or_11 (or_11_out, cycle_counter_1_instruction_end, RESET);
  assign or_12_out = or_14_out[4:0] | or_16_out[4:0] | multiplexer_5_out;  // OR_Gate or_12, 5 bits wide
  Button button_3 (.out(button_3_out));
  LedBar #(.matrixcols(4)) ledbar_16 (.led0(undriven[3]), .led1(undriven[2]), .led2(undriven[1]), .led3(undriven[0]));
  DipSwitch #(.number(16)) dipswitch_2 (
    .sw1(dipswitch_2_sw16[15]), .sw2(dipswitch_2_sw16[14]), .sw3(dipswitch_2_sw16[13]),
    .sw4(dipswitch_2_sw16[12]), .sw5(dipswitch_2_sw16[11]), .sw6(dipswitch_2_sw16[10]),
    .sw7(dipswitch_2_sw16[9]), .sw8(dipswitch_2_sw16[8]), .sw9(dipswitch_2_sw16[7]),
    .sw10(dipswitch_2_sw16[6]), .sw11(dipswitch_2_sw16[5]), .sw12(dipswitch_2_sw16[4]),
    .sw13(dipswitch_2_sw16[3]), .sw14(dipswitch_2_sw16[2]), .sw15(dipswitch_2_sw16[1]),
    .sw16(dipswitch_2_sw16[0]));
  DipSwitch #(.number(16)) dipswitch_3 (
    .sw1(dipswitch_3_sw16[15]), .sw2(dipswitch_3_sw16[14]), .sw3(dipswitch_3_sw16[13]),
    .sw4(dipswitch_3_sw16[12]), .sw5(dipswitch_3_sw16[11]), .sw6(dipswitch_3_sw16[10]),
    .sw7(dipswitch_3_sw16[9]), .sw8(dipswitch_3_sw16[8]), .sw9(dipswitch_3_sw16[7]),
    .sw10(dipswitch_3_sw16[6]), .sw11(dipswitch_3_sw16[5]), .sw12(dipswitch_3_sw16[4]),
    .sw13(dipswitch_3_sw16[3]), .sw14(dipswitch_3_sw16[2]), .sw15(dipswitch_3_sw16[1]),
    .sw16(dipswitch_3_sw16[0]));
  DipSwitch #(.number(16)) dipswitch_4 (
    .sw1(dipswitch_4_sw16[15]), .sw2(dipswitch_4_sw16[14]), .sw3(dipswitch_4_sw16[13]),
    .sw4(dipswitch_4_sw16[12]), .sw5(dipswitch_4_sw16[11]), .sw6(dipswitch_4_sw16[10]),
    .sw7(dipswitch_4_sw16[9]), .sw8(dipswitch_4_sw16[8]), .sw9(dipswitch_4_sw16[7]),
    .sw10(dipswitch_4_sw16[6]), .sw11(dipswitch_4_sw16[5]), .sw12(dipswitch_4_sw16[4]),
    .sw13(dipswitch_4_sw16[3]), .sw14(dipswitch_4_sw16[2]), .sw15(dipswitch_4_sw16[1]),
    .sw16(dipswitch_4_sw16[0]));
  DipSwitch #(.number(16)) dipswitch_5 (
    .sw1(dipswitch_5_sw16[15]), .sw2(dipswitch_5_sw16[14]), .sw3(dipswitch_5_sw16[13]),
    .sw4(dipswitch_5_sw16[12]), .sw5(dipswitch_5_sw16[11]), .sw6(dipswitch_5_sw16[10]),
    .sw7(dipswitch_5_sw16[9]), .sw8(dipswitch_5_sw16[8]), .sw9(dipswitch_5_sw16[7]),
    .sw10(dipswitch_5_sw16[6]), .sw11(dipswitch_5_sw16[5]), .sw12(dipswitch_5_sw16[4]),
    .sw13(dipswitch_5_sw16[3]), .sw14(dipswitch_5_sw16[2]), .sw15(dipswitch_5_sw16[1]),
    .sw16(dipswitch_5_sw16[0]));
  DipSwitch #(.number(16)) dipswitch_6 (
    .sw1(dipswitch_6_sw16[15]), .sw2(dipswitch_6_sw16[14]), .sw3(dipswitch_6_sw16[13]),
    .sw4(dipswitch_6_sw16[12]), .sw5(dipswitch_6_sw16[11]), .sw6(dipswitch_6_sw16[10]),
    .sw7(dipswitch_6_sw16[9]), .sw8(dipswitch_6_sw16[8]), .sw9(dipswitch_6_sw16[7]),
    .sw10(dipswitch_6_sw16[6]), .sw11(dipswitch_6_sw16[5]), .sw12(dipswitch_6_sw16[4]),
    .sw13(dipswitch_6_sw16[3]), .sw14(dipswitch_6_sw16[2]), .sw15(dipswitch_6_sw16[1]),
    .sw16(dipswitch_6_sw16[0]));
  DipSwitch #(.number(16)) dipswitch_7 (
    .sw1(dipswitch_7_sw16[15]), .sw2(dipswitch_7_sw16[14]), .sw3(dipswitch_7_sw16[13]),
    .sw4(dipswitch_7_sw16[12]), .sw5(dipswitch_7_sw16[11]), .sw6(dipswitch_7_sw16[10]),
    .sw7(dipswitch_7_sw16[9]), .sw8(dipswitch_7_sw16[8]), .sw9(dipswitch_7_sw16[7]),
    .sw10(dipswitch_7_sw16[6]), .sw11(dipswitch_7_sw16[5]), .sw12(dipswitch_7_sw16[4]),
    .sw13(dipswitch_7_sw16[3]), .sw14(dipswitch_7_sw16[2]), .sw15(dipswitch_7_sw16[1]),
    .sw16(dipswitch_7_sw16[0]));
  DipSwitch #(.number(16)) dipswitch_8 (
    .sw1(dipswitch_8_sw16[15]), .sw2(dipswitch_8_sw16[14]), .sw3(dipswitch_8_sw16[13]),
    .sw4(dipswitch_8_sw16[12]), .sw5(dipswitch_8_sw16[11]), .sw6(dipswitch_8_sw16[10]),
    .sw7(dipswitch_8_sw16[9]), .sw8(dipswitch_8_sw16[8]), .sw9(dipswitch_8_sw16[7]),
    .sw10(dipswitch_8_sw16[6]), .sw11(dipswitch_8_sw16[5]), .sw12(dipswitch_8_sw16[4]),
    .sw13(dipswitch_8_sw16[3]), .sw14(dipswitch_8_sw16[2]), .sw15(dipswitch_8_sw16[1]),
    .sw16(dipswitch_8_sw16[0]));
  DipSwitch #(.number(16)) dipswitch_9 (
    .sw1(dipswitch_9_sw16[15]), .sw2(dipswitch_9_sw16[14]), .sw3(dipswitch_9_sw16[13]),
    .sw4(dipswitch_9_sw16[12]), .sw5(dipswitch_9_sw16[11]), .sw6(dipswitch_9_sw16[10]),
    .sw7(dipswitch_9_sw16[9]), .sw8(dipswitch_9_sw16[8]), .sw9(dipswitch_9_sw16[7]),
    .sw10(dipswitch_9_sw16[6]), .sw11(dipswitch_9_sw16[5]), .sw12(dipswitch_9_sw16[4]),
    .sw13(dipswitch_9_sw16[3]), .sw14(dipswitch_9_sw16[2]), .sw15(dipswitch_9_sw16[1]),
    .sw16(dipswitch_9_sw16[0]));
  DipSwitch #(.number(16)) dipswitch_10 (
    .sw1(dipswitch_10_sw16[15]), .sw2(dipswitch_10_sw16[14]), .sw3(dipswitch_10_sw16[13]),
    .sw4(dipswitch_10_sw16[12]), .sw5(dipswitch_10_sw16[11]), .sw6(dipswitch_10_sw16[10]),
    .sw7(dipswitch_10_sw16[9]), .sw8(dipswitch_10_sw16[8]), .sw9(dipswitch_10_sw16[7]),
    .sw10(dipswitch_10_sw16[6]), .sw11(dipswitch_10_sw16[5]), .sw12(dipswitch_10_sw16[4]),
    .sw13(dipswitch_10_sw16[3]), .sw14(dipswitch_10_sw16[2]), .sw15(dipswitch_10_sw16[1]),
    .sw16(dipswitch_10_sw16[0]));
  DipSwitch #(.number(16)) dipswitch_11 (
    .sw1(dipswitch_11_sw16[15]), .sw2(dipswitch_11_sw16[14]), .sw3(dipswitch_11_sw16[13]),
    .sw4(dipswitch_11_sw16[12]), .sw5(dipswitch_11_sw16[11]), .sw6(dipswitch_11_sw16[10]),
    .sw7(dipswitch_11_sw16[9]), .sw8(dipswitch_11_sw16[8]), .sw9(dipswitch_11_sw16[7]),
    .sw10(dipswitch_11_sw16[6]), .sw11(dipswitch_11_sw16[5]), .sw12(dipswitch_11_sw16[4]),
    .sw13(dipswitch_11_sw16[3]), .sw14(dipswitch_11_sw16[2]), .sw15(dipswitch_11_sw16[1]),
    .sw16(dipswitch_11_sw16[0]));
  DipSwitch #(.number(16)) dipswitch_12 (
    .sw1(dipswitch_12_sw16[15]), .sw2(dipswitch_12_sw16[14]), .sw3(dipswitch_12_sw16[13]),
    .sw4(dipswitch_12_sw16[12]), .sw5(dipswitch_12_sw16[11]), .sw6(dipswitch_12_sw16[10]),
    .sw7(dipswitch_12_sw16[9]), .sw8(dipswitch_12_sw16[8]), .sw9(dipswitch_12_sw16[7]),
    .sw10(dipswitch_12_sw16[6]), .sw11(dipswitch_12_sw16[5]), .sw12(dipswitch_12_sw16[4]),
    .sw13(dipswitch_12_sw16[3]), .sw14(dipswitch_12_sw16[2]), .sw15(dipswitch_12_sw16[1]),
    .sw16(dipswitch_12_sw16[0]));
  DipSwitch #(.number(16)) dipswitch_13 (
    .sw1(dipswitch_13_sw16[15]), .sw2(dipswitch_13_sw16[14]), .sw3(dipswitch_13_sw16[13]),
    .sw4(dipswitch_13_sw16[12]), .sw5(dipswitch_13_sw16[11]), .sw6(dipswitch_13_sw16[10]),
    .sw7(dipswitch_13_sw16[9]), .sw8(dipswitch_13_sw16[8]), .sw9(dipswitch_13_sw16[7]),
    .sw10(dipswitch_13_sw16[6]), .sw11(dipswitch_13_sw16[5]), .sw12(dipswitch_13_sw16[4]),
    .sw13(dipswitch_13_sw16[3]), .sw14(dipswitch_13_sw16[2]), .sw15(dipswitch_13_sw16[1]),
    .sw16(dipswitch_13_sw16[0]));
  DipSwitch #(.number(16)) dipswitch_14 (
    .sw1(dipswitch_14_sw16[15]), .sw2(dipswitch_14_sw16[14]), .sw3(dipswitch_14_sw16[13]),
    .sw4(dipswitch_14_sw16[12]), .sw5(dipswitch_14_sw16[11]), .sw6(dipswitch_14_sw16[10]),
    .sw7(dipswitch_14_sw16[9]), .sw8(dipswitch_14_sw16[8]), .sw9(dipswitch_14_sw16[7]),
    .sw10(dipswitch_14_sw16[6]), .sw11(dipswitch_14_sw16[5]), .sw12(dipswitch_14_sw16[4]),
    .sw13(dipswitch_14_sw16[3]), .sw14(dipswitch_14_sw16[2]), .sw15(dipswitch_14_sw16[1]),
    .sw16(dipswitch_14_sw16[0]));
  DipSwitch #(.number(16)) dipswitch_15 (
    .sw1(dipswitch_15_sw16[15]), .sw2(dipswitch_15_sw16[14]), .sw3(dipswitch_15_sw16[13]),
    .sw4(dipswitch_15_sw16[12]), .sw5(dipswitch_15_sw16[11]), .sw6(dipswitch_15_sw16[10]),
    .sw7(dipswitch_15_sw16[9]), .sw8(dipswitch_15_sw16[8]), .sw9(dipswitch_15_sw16[7]),
    .sw10(dipswitch_15_sw16[6]), .sw11(dipswitch_15_sw16[5]), .sw12(dipswitch_15_sw16[4]),
    .sw13(dipswitch_15_sw16[3]), .sw14(dipswitch_15_sw16[2]), .sw15(dipswitch_15_sw16[1]),
    .sw16(dipswitch_15_sw16[0]));
  DipSwitch #(.number(16)) dipswitch_16 (
    .sw1(dipswitch_16_sw16[15]), .sw2(dipswitch_16_sw16[14]), .sw3(dipswitch_16_sw16[13]),
    .sw4(dipswitch_16_sw16[12]), .sw5(dipswitch_16_sw16[11]), .sw6(dipswitch_16_sw16[10]),
    .sw7(dipswitch_16_sw16[9]), .sw8(dipswitch_16_sw16[8]), .sw9(dipswitch_16_sw16[7]),
    .sw10(dipswitch_16_sw16[6]), .sw11(dipswitch_16_sw16[5]), .sw12(dipswitch_16_sw16[4]),
    .sw13(dipswitch_16_sw16[3]), .sw14(dipswitch_16_sw16[2]), .sw15(dipswitch_16_sw16[1]),
    .sw16(dipswitch_16_sw16[0]));
  LedBar #(.matrixcols(16)) ledbar_17 (
    .led0(undriven_2[15]), .led1(undriven_2[14]), .led2(undriven_2[13]), .led3(undriven_2[12]),
    .led4(undriven_2[11]), .led5(undriven_2[10]), .led6(undriven_2[9]), .led7(undriven_2[8]),
    .led8(undriven_2[7]), .led9(undriven_2[6]), .led10(undriven_2[5]), .led11(undriven_2[4]),
    .led12(undriven_2[3]), .led13(undriven_2[2]), .led14(undriven_2[1]), .led15(undriven_2[0]));
  Cycle_Counter cycle_counter_1 (
    .ADRESS(indirect_adressing_unit_1_output_0), .CLK(clock_kronos_1_clock_out),
    .INSTRUCTION_READY(indirect_adressing_unit_1_instruction_ready_out), .RESET(or_10_out),
    .INSTRUCTION_END(cycle_counter_1_instruction_end),
    .INSTRUCTION_STATE_2(cycle_counter_1_instruction_state_2));
  Indirect_Adressing_Unit indirect_adressing_unit_1 (
    .RESET(or_11_out), .CLK(clock_kronos_1_clock_out), .DATA_0(instruction_fetch_buffer_1_output_0),
    .DATA_1(instruction_fetch_buffer_1_output_1), .DATA_2(instruction_fetch_buffer_1_output_2),
    .INSTRUCTION_READY_IN(instruction_fetch_buffer_1_instruction_ready),
    .INPUT_REG(register_type32_1_data_0), .INPUT_RAM(multiplexer_2_out),
    .OUTPUT_0({indirect_adressing_unit_1_output_0_2, indirect_adressing_unit_1_output_0}),
    .OUTPUT_1(indirect_adressing_unit_1_output_1), .OUTPUT_2(indirect_adressing_unit_1_output_2),
    .INSTRUCTION_READY_OUT(indirect_adressing_unit_1_instruction_ready_out),
    .REG_ADRESS(indirect_adressing_unit_1_reg_adress), .RAM_ADRESS(indirect_adressing_unit_1_ram_adress),
    .READ_RAM(indirect_adressing_unit_1_read_ram));
  assign or_13_out = or_21_out | demultiplexer_10_out0[4:0] | or_16_out[14:10] | demultiplexer_4_out0;  // OR_Gate or_13, 5 bits wide
  assign or_14_out = demultiplexer_2_out1 | demultiplexer_2_out2 | demultiplexer_2_out5 | demultiplexer_2_out6 | demultiplexer_2_out7 | demultiplexer_2_out9 | demultiplexer_2_out10 | demultiplexer_2_out11 | demultiplexer_2_out12 | demultiplexer_2_out13 | demultiplexer_2_out14;  // OR_Gate or_14, 16 bits wide
  assign or_15_out = indirect_adressing_unit_1_ram_adress | demultiplexer_6_out1 | demultiplexer_4_out1 | multiplexer_3_out;  // OR_Gate or_15, 15 bits wide
  Demultiplexer #(.select(5), .width(16)) demultiplexer_2 (
    .out1(demultiplexer_2_out1), .out2(demultiplexer_2_out2), .out3(demultiplexer_2_out3),
    .out4(demultiplexer_2_out4), .out5(demultiplexer_2_out5), .out6(demultiplexer_2_out6),
    .out7(demultiplexer_2_out7), .out8(demultiplexer_2_out8), .out9(demultiplexer_2_out9),
    .out10(demultiplexer_2_out10), .out11(demultiplexer_2_out11), .out12(demultiplexer_2_out12),
    .out13(demultiplexer_2_out13), .out14(demultiplexer_2_out14), .out16(demultiplexer_2_out16),
    .out18(demultiplexer_2_out18), .out19(demultiplexer_2_out19),
    .in({indirect_adressing_unit_1_output_0_2, indirect_adressing_unit_1_output_0}),
    .sel(indirect_adressing_unit_1_output_0));  // open: out0, out15, out17, out20, out21, out22, out23, out24, out25, out26, out27, out28, out29, out30, out31
  assign or_16_out = demultiplexer_2_out3 | demultiplexer_2_out4 | demultiplexer_2_out8;  // OR_Gate or_16, 16 bits wide
  assign or_17_out = demultiplexer_2_out16;  // OR_Gate or_17, 16 bits wide OR_Gate
  Multiplexer #(.width(5)) multiplexer_5 (
    .in0({5{1'b0}}), .in1(5'b01001), .out(multiplexer_5_out), .sel(demultiplexer_11_out16));
  assign or_18_out = or_25_out;  // OR_Gate or_18, 16 bits wide OR_Gate
  Inputs inputs_1 (
    .ADRESS(demultiplexer_2_out19[8:5]), .CLK(clock_kronos_1_clock_out), .INPUT_1(dipswitch_2_sw16),
    .INPUT_2(dipswitch_3_sw16), .INPUT_3(dipswitch_4_sw16), .INPUT_4(dipswitch_5_sw16),
    .INPUT_5(dipswitch_6_sw16), .INPUT_6(dipswitch_7_sw16), .INPUT_7(dipswitch_8_sw16),
    .INPUT_8(dipswitch_9_sw16), .INPUT_9(dipswitch_10_sw16), .INPUT_10(dipswitch_11_sw16),
    .INPUT_11(dipswitch_12_sw16), .INPUT_12(dipswitch_13_sw16), .INPUT_13(dipswitch_14_sw16),
    .INPUT_14(dipswitch_15_sw16), .INPUT_15(dipswitch_16_sw16), .DATA_OUT(inputs_1_data_out));
  assign or_19_out = alu_1_data_out | stack_1_output_stack | register_1_q | demultiplexer_9_out0 | demultiplexer_3_out0 | register_1_q;  // OR_Gate or_19, 16 bits wide
  Demultiplexer #(.width(16)) demultiplexer_3 (
    .out0(demultiplexer_3_out0), .out1(demultiplexer_3_out1), .in(inputs_1_data_out), .sel(or_23_out[0]));
  and and_5 (and_5_out, cycle_counter_1_instruction_state_2, demultiplexer_11_out21);
  and and_6 (and_6_out, cycle_counter_1_instruction_state_2, demultiplexer_11_out22);
  assign or_20_out = demultiplexer_9_out1 | stack_1_output_stack | register_1_q | register_1_q | demultiplexer_3_out1;  // OR_Gate or_20, 16 bits wide
  assign {or_21_out_2, or_21_out} = demultiplexer_5_out1 | demultiplexer_5_out2 | demultiplexer_5_out5 | demultiplexer_5_out6 | demultiplexer_5_out7 | demultiplexer_5_out9 | demultiplexer_5_out10 | demultiplexer_5_out11 | demultiplexer_5_out12 | demultiplexer_5_out13 | demultiplexer_5_out14;  // OR_Gate or_21, 16 bits wide
  or or_22 (or_22_out, demultiplexer_1_out1, demultiplexer_12_out1);
  Stack stack_1 (
    .RESET(RESET), .PUSH(and_5_out), .POP(and_6_out), .CLK(clock_kronos_1_clock_out),
    .READ(demultiplexer_11_out23), .DATA_IN(or_29_out), .OUTPUT_STACK(stack_1_output_stack));
  Demultiplexer #(.width(15)) demultiplexer_4 (
    .out0({demultiplexer_4_out0_2, demultiplexer_4_out0}), .out1(demultiplexer_4_out1), .in(or_23_out_2),
    .sel(or_23_out[0]));
  Demultiplexer #(.select(5), .width(16)) demultiplexer_5 (
    .out1(demultiplexer_5_out1), .out2(demultiplexer_5_out2), .out5(demultiplexer_5_out5),
    .out6(demultiplexer_5_out6), .out7(demultiplexer_5_out7), .out9(demultiplexer_5_out9),
    .out10(demultiplexer_5_out10), .out11(demultiplexer_5_out11), .out12(demultiplexer_5_out12),
    .out13(demultiplexer_5_out13), .out14(demultiplexer_5_out14), .out15(demultiplexer_5_out15),
    .out16(demultiplexer_5_out16), .out17(demultiplexer_5_out17), .out18(demultiplexer_5_out18),
    .out19(demultiplexer_5_out19), .out20(demultiplexer_5_out20), .out21(demultiplexer_5_out21),
    .out23(demultiplexer_5_out23), .in(indirect_adressing_unit_1_output_1),
    .sel(indirect_adressing_unit_1_output_0));  // open: out0, out3, out4, out8, out22, out24, out25, out26, out27, out28, out29, out30, out31
  assign {or_23_out_2, or_23_out[0]} = demultiplexer_5_out15 | demultiplexer_5_out19 | demultiplexer_5_out23;  // OR_Gate or_23, 16 bits wide
  or or_24 (or_24_out, multiplexer_1_out, demultiplexer_11_out17);
  assign or_25_out = demultiplexer_5_out16 | demultiplexer_5_out17;  // OR_Gate or_25, 16 bits wide
  Demultiplexer #(.width(15)) demultiplexer_6 (
    .out0(demultiplexer_6_out0), .out1(demultiplexer_6_out1), .in(or_26_out), .sel(or_26_out_2[0]));
  assign {or_26_out, or_26_out_2[0]} = demultiplexer_5_out21 | demultiplexer_5_out18;  // OR_Gate or_26, 16 bits wide
  Demultiplexer #(.width(15)) demultiplexer_7 (
    .out0(demultiplexer_7_out0), .out1(demultiplexer_7_out1), .in(demultiplexer_5_out20[15:1]),
    .sel(demultiplexer_5_out20[0]));
  assign or_27_out = demultiplexer_2_out18[8:5];  // OR_Gate or_27, 4 bits wide OR_Gate
  or or_28 (or_28_out, multiplexer_4_out, or_26_out_2[0], indirect_adressing_unit_1_read_ram);
  Demultiplexer #(.select(5), .width(16)) demultiplexer_8 (
    .out15(demultiplexer_8_out15), .out20(demultiplexer_8_out20), .in(indirect_adressing_unit_1_output_2),
    .sel(indirect_adressing_unit_1_output_0));  // open: out0, out1, out2, out3, out4, out5, out6, out7, out8, out9, out10, out11, out12, out13, out14, out16, out17, out18, out19, out21, out22, out23, out24, out25, out26, out27, out28, out29, out30, out31
  Demultiplexer #(.width(16)) demultiplexer_9 (
    .out0(demultiplexer_9_out0), .out1(demultiplexer_9_out1), .in(demultiplexer_8_out15), .sel(or_23_out[0]));
  Demultiplexer #(.width(15)) demultiplexer_10 (
    .out0(demultiplexer_10_out0), .out1(demultiplexer_10_out1), .in(demultiplexer_8_out20[15:1]),
    .sel(demultiplexer_8_out20[0]));
  assign or_29_out = or_6_out;  // OR_Gate or_29, 16 bits wide OR_Gate
  Demultiplexer #(.select(5)) demultiplexer_11 (
    .out1(demultiplexer_11_out1), .out2(demultiplexer_11_out2), .out3(demultiplexer_11_out3),
    .out4(demultiplexer_11_out4), .out5(demultiplexer_11_out5), .out6(demultiplexer_11_out6),
    .out7(demultiplexer_11_out7), .out8(demultiplexer_11_out8), .out9(demultiplexer_11_out9),
    .out10(demultiplexer_11_out10), .out11(demultiplexer_11_out11), .out12(demultiplexer_11_out12),
    .out13(demultiplexer_11_out13), .out14(demultiplexer_11_out14), .out15(demultiplexer_11_out15),
    .out16(demultiplexer_11_out16), .out17(demultiplexer_11_out17), .out18(demultiplexer_11_out18),
    .out19(demultiplexer_11_out19), .out20(demultiplexer_11_out20), .out21(demultiplexer_11_out21),
    .out22(demultiplexer_11_out22), .out23(demultiplexer_11_out23), .in(1'b1),
    .sel(indirect_adressing_unit_1_output_0));  // open: out0, out24, out25, out26, out27, out28, out29, out30, out31
  or or_30 (or_30_out, demultiplexer_11_out1, demultiplexer_11_out2, demultiplexer_11_out3, demultiplexer_11_out4, demultiplexer_11_out5, demultiplexer_11_out6, demultiplexer_11_out7, demultiplexer_11_out9, demultiplexer_11_out10, demultiplexer_11_out11, demultiplexer_11_out12, demultiplexer_11_out13, demultiplexer_11_out14, demultiplexer_11_out8, demultiplexer_1_out0, demultiplexer_12_out0);
  or or_31 (or_31_out, demultiplexer_11_out15, demultiplexer_11_out19, demultiplexer_11_out23);
  Demultiplexer demultiplexer_12 (
    .out0(demultiplexer_12_out0), .out1(demultiplexer_12_out1), .in(or_31_out), .sel(or_23_out[0]));

  // Notes on the sheet:
  //   contents of rom_1 (hex, n*v repeats v):
  //   430 a
  //   READ_1
  //   READ_0
  //   OPCODE_ALU
  //   ADRESS_REGISTER
  //   ADRESS_RAM
  //   JUMP_ADRESS
  //   DATA_IN_REGISTER
  //   DATA_IN_RAM
  //   WRITE_RAM
  //   JUMP
  //   OUTPUT_ADRESS
  //   READ_RAM
  //   STACK_DATA_IN
  //   WRITE_REGISTER
endmodule
