// Logisim project Outputs.circ as structural Verilog: 1 circuit, main circuit Outputs
module Outputs (
  input  RESET,
  input  WRITE,
  input  [3:0] OUTPUT_ADRESS,
  input  [15:0] DATA_IN,
  input  CLK,
  output [15:0] OUTPUT_1,
  output [15:0] OUTPUT_2,
  output [15:0] OUTPUT_3,
  output [15:0] OUTPUT_4,
  output [15:0] OUTPUT_5,
  output [15:0] OUTPUT_6,
  output [15:0] OUTPUT_7,
  output [15:0] OUTPUT_8,
  output [15:0] OUTPUT_9,
  output [15:0] OUTPUT_10,
  output [15:0] OUTPUT_11,
  output [15:0] OUTPUT_12,
  output [15:0] OUTPUT_13,
  output [15:0] OUTPUT_14,
  output [15:0] OUTPUT_15
);

  wire adress_comparator_4bit_1_output_adress, adress_comparator_4bit_2_output_adress,
       adress_comparator_4bit_3_output_adress, adress_comparator_4bit_4_output_adress,
       adress_comparator_4bit_5_output_adress, adress_comparator_4bit_6_output_adress,
       adress_comparator_4bit_7_output_adress, adress_comparator_4bit_8_output_adress,
       adress_comparator_4bit_9_output_adress, adress_comparator_4bit_10_output_adress,
       adress_comparator_4bit_11_output_adress, adress_comparator_4bit_12_output_adress,
       adress_comparator_4bit_13_output_adress, adress_comparator_4bit_14_output_adress,
       adress_comparator_4bit_15_output_adress, and_1_out, and_2_out, and_3_out, and_4_out, and_5_out,
       and_6_out, and_7_out, and_8_out, and_9_out, and_10_out, and_11_out, and_12_out, and_13_out,
       and_14_out, and_15_out, d_ff_1_q, d_ff_2_q;

  D_Flip_Flop d_ff_1 (.D(RESET), .clk(CLK), .Q(d_ff_1_q));  // open: Qn, preset, reset
  D_Flip_Flop d_ff_2 (.D(WRITE), .clk(CLK), .Q(d_ff_2_q));  // open: Qn, preset, reset
  Adress_Comparator_4bit adress_comparator_4bit_1 (
    .ADRESS(OUTPUT_ADRESS), .PHYSICAL_ADRESS(4'b0001), .OUTPUT_ADRESS(adress_comparator_4bit_1_output_adress));
  Adress_Comparator_4bit adress_comparator_4bit_2 (
    .ADRESS(OUTPUT_ADRESS), .PHYSICAL_ADRESS(4'b0010), .OUTPUT_ADRESS(adress_comparator_4bit_2_output_adress));
  Adress_Comparator_4bit adress_comparator_4bit_3 (
    .ADRESS(OUTPUT_ADRESS), .PHYSICAL_ADRESS(4'b0011), .OUTPUT_ADRESS(adress_comparator_4bit_3_output_adress));
  Adress_Comparator_4bit adress_comparator_4bit_4 (
    .ADRESS(OUTPUT_ADRESS), .PHYSICAL_ADRESS(4'b0100), .OUTPUT_ADRESS(adress_comparator_4bit_4_output_adress));
  Adress_Comparator_4bit adress_comparator_4bit_5 (
    .ADRESS(OUTPUT_ADRESS), .PHYSICAL_ADRESS(4'b0101), .OUTPUT_ADRESS(adress_comparator_4bit_5_output_adress));
  Adress_Comparator_4bit adress_comparator_4bit_6 (
    .ADRESS(OUTPUT_ADRESS), .PHYSICAL_ADRESS(4'b0110), .OUTPUT_ADRESS(adress_comparator_4bit_6_output_adress));
  Adress_Comparator_4bit adress_comparator_4bit_7 (
    .ADRESS(OUTPUT_ADRESS), .PHYSICAL_ADRESS(4'b0111), .OUTPUT_ADRESS(adress_comparator_4bit_7_output_adress));
  Adress_Comparator_4bit adress_comparator_4bit_8 (
    .ADRESS(OUTPUT_ADRESS), .PHYSICAL_ADRESS(4'b1000), .OUTPUT_ADRESS(adress_comparator_4bit_8_output_adress));
  Adress_Comparator_4bit adress_comparator_4bit_9 (
    .ADRESS(OUTPUT_ADRESS), .PHYSICAL_ADRESS(4'b1001), .OUTPUT_ADRESS(adress_comparator_4bit_9_output_adress));
  Adress_Comparator_4bit adress_comparator_4bit_10 (
    .ADRESS(OUTPUT_ADRESS), .PHYSICAL_ADRESS(4'b1010), .OUTPUT_ADRESS(adress_comparator_4bit_10_output_adress));
  Adress_Comparator_4bit adress_comparator_4bit_11 (
    .ADRESS(OUTPUT_ADRESS), .PHYSICAL_ADRESS(4'b1011), .OUTPUT_ADRESS(adress_comparator_4bit_11_output_adress));
  Adress_Comparator_4bit adress_comparator_4bit_12 (
    .ADRESS(OUTPUT_ADRESS), .PHYSICAL_ADRESS(4'b1100), .OUTPUT_ADRESS(adress_comparator_4bit_12_output_adress));
  Adress_Comparator_4bit adress_comparator_4bit_13 (
    .ADRESS(OUTPUT_ADRESS), .PHYSICAL_ADRESS(4'b1101), .OUTPUT_ADRESS(adress_comparator_4bit_13_output_adress));
  Adress_Comparator_4bit adress_comparator_4bit_14 (
    .ADRESS(OUTPUT_ADRESS), .PHYSICAL_ADRESS(4'b1110), .OUTPUT_ADRESS(adress_comparator_4bit_14_output_adress));
  Adress_Comparator_4bit adress_comparator_4bit_15 (
    .ADRESS(OUTPUT_ADRESS), .PHYSICAL_ADRESS(4'b1111), .OUTPUT_ADRESS(adress_comparator_4bit_15_output_adress));
  and and_1 (and_1_out, CLK, d_ff_2_q, adress_comparator_4bit_1_output_adress);
  and and_2 (and_2_out, CLK, d_ff_2_q, adress_comparator_4bit_2_output_adress);
  and and_3 (and_3_out, CLK, d_ff_2_q, adress_comparator_4bit_3_output_adress);
  and and_4 (and_4_out, CLK, d_ff_2_q, adress_comparator_4bit_4_output_adress);
  and and_5 (and_5_out, CLK, d_ff_2_q, adress_comparator_4bit_5_output_adress);
  and and_6 (and_6_out, CLK, d_ff_2_q, adress_comparator_4bit_6_output_adress);
  and and_7 (and_7_out, CLK, d_ff_2_q, adress_comparator_4bit_7_output_adress);
  and and_8 (and_8_out, CLK, d_ff_2_q, adress_comparator_4bit_8_output_adress);
  and and_9 (and_9_out, CLK, d_ff_2_q, adress_comparator_4bit_9_output_adress);
  and and_10 (and_10_out, CLK, d_ff_2_q, adress_comparator_4bit_10_output_adress);
  and and_11 (and_11_out, CLK, d_ff_2_q, adress_comparator_4bit_11_output_adress);
  and and_12 (and_12_out, CLK, d_ff_2_q, adress_comparator_4bit_12_output_adress);
  and and_13 (and_13_out, CLK, d_ff_2_q, adress_comparator_4bit_13_output_adress);
  and and_14 (and_14_out, CLK, d_ff_2_q, adress_comparator_4bit_14_output_adress);
  and and_15 (and_15_out, CLK, d_ff_2_q, adress_comparator_4bit_15_output_adress);
  Register #(.width(16)) register_1 (.D(DATA_IN), .en(1'b1), .clk(and_1_out), .Q(OUTPUT_1), .clr(d_ff_1_q));
  Register #(.width(16)) register_2 (.D(DATA_IN), .en(1'b1), .clk(and_2_out), .Q(OUTPUT_2), .clr(d_ff_1_q));
  Register #(.width(16)) register_3 (.D(DATA_IN), .en(1'b1), .clk(and_3_out), .Q(OUTPUT_3), .clr(d_ff_1_q));
  Register #(.width(16)) register_4 (.D(DATA_IN), .en(1'b1), .clk(and_4_out), .Q(OUTPUT_4), .clr(d_ff_1_q));
  Register #(.width(16)) register_5 (.D(DATA_IN), .en(1'b1), .clk(and_5_out), .Q(OUTPUT_5), .clr(d_ff_1_q));
  Register #(.width(16)) register_6 (.D(DATA_IN), .en(1'b1), .clk(and_6_out), .Q(OUTPUT_6), .clr(d_ff_1_q));
  Register #(.width(16)) register_7 (.D(DATA_IN), .en(1'b1), .clk(and_7_out), .Q(OUTPUT_7), .clr(d_ff_1_q));
  Register #(.width(16)) register_8 (.D(DATA_IN), .en(1'b1), .clk(and_8_out), .Q(OUTPUT_8), .clr(d_ff_1_q));
  Register #(.width(16)) register_9 (.D(DATA_IN), .en(1'b1), .clk(and_9_out), .Q(OUTPUT_9), .clr(d_ff_1_q));
  Register #(.width(16)) register_10 (.D(DATA_IN), .en(1'b1), .clk(and_10_out), .Q(OUTPUT_10), .clr(d_ff_1_q));
  Register #(.width(16)) register_11 (.D(DATA_IN), .en(1'b1), .clk(and_11_out), .Q(OUTPUT_11), .clr(d_ff_1_q));
  Register #(.width(16)) register_12 (.D(DATA_IN), .en(1'b1), .clk(and_12_out), .Q(OUTPUT_12), .clr(d_ff_1_q));
  Register #(.width(16)) register_13 (.D(DATA_IN), .en(1'b1), .clk(and_13_out), .Q(OUTPUT_13), .clr(d_ff_1_q));
  Register #(.width(16)) register_14 (.D(DATA_IN), .en(1'b1), .clk(and_14_out), .Q(OUTPUT_14), .clr(d_ff_1_q));
  Register #(.width(16)) register_15 (.D(DATA_IN), .en(1'b1), .clk(and_15_out), .Q(OUTPUT_15), .clr(d_ff_1_q));
endmodule
