// Logisim project Program_Counter.circ as structural Verilog: 1 circuit, main circuit Program_Counter
module Program_Counter (
  input  [15:0] ADRESS,
  input  NEXT_INSTRUCTION,
  input  JUMP,
  input  CLK,
  input  RESET,
  output [15:0] out_6
);

  wire and_1_out, and_2_out, and_3_out, d_ff_1_q, d_ff_2_q, d_ff_3_q, xor_1_out;
  wire [1:0] multiplexer_1_out, multiplexer_2_out, multiplexer_3_out, xor_2_out;
  wire [15:0] adder_1_out, multiplexer_4_out;

  D_Flip_Flop d_ff_1 (.D(NEXT_INSTRUCTION), .clk(CLK), .Q(d_ff_1_q), .reset(d_ff_3_q));  // open: Qn, preset
  D_Flip_Flop d_ff_2 (.D(JUMP), .clk(CLK), .Q(d_ff_2_q), .reset(d_ff_3_q));  // open: Qn, preset
  D_Flip_Flop d_ff_3 (.D(RESET), .clk(CLK), .Q(d_ff_3_q), .reset(d_ff_3_q));  // open: Qn, preset
  Multiplexer #(.width(2)) multiplexer_1 (.in0(2'b00), .in1(2'b01), .out(multiplexer_1_out), .sel(NEXT_INSTRUCTION));
  Multiplexer #(.width(2)) multiplexer_2 (.in0(2'b00), .in1(2'b10), .out(multiplexer_2_out), .sel(JUMP));
  and and_1 (and_1_out, NEXT_INSTRUCTION, JUMP);
  xor xor_1 (xor_1_out, d_ff_1_q, d_ff_2_q);
  and and_2 (and_2_out, CLK, d_ff_3_q);
  assign xor_2_out = multiplexer_1_out ^ multiplexer_2_out;  // XOR_Gate xor_2, 2 bits wide
  Multiplexer #(.width(2)) multiplexer_3 (.in0(xor_2_out), .in1(2'b00), .out(multiplexer_3_out), .sel(and_1_out));
  and and_3 (and_3_out, xor_1_out, CLK);
  Multiplexer #(.select(2), .width(16)) multiplexer_4 (
    .in0(out_6), .in1(adder_1_out), .in2(ADRESS), .in3(out_6), .out(multiplexer_4_out),
    .sel(multiplexer_3_out));
  Adder #(.width(16)) adder_1 (.a(out_6), .b({16{1'b0}}), .out(adder_1_out), .cin(1'b1));  // open: cout
  Register #(.width(16)) register_1 (.D(multiplexer_4_out), .en(1'b1), .clk(and_3_out), .Q(out_6), .clr(and_2_out));
endmodule
