// Logisim project Register_Type32_16bit.circ as structural Verilog: 1 circuit, main circuit Register_Type32
module Register_Type32 (
  input  CLK,
  input  WRITE,
  input  [15:0] DATA_IN,
  input  [4:0] WRITE_ADRESS,
  input  [4:0] READ_0,
  input  [4:0] READ_1,
  output [15:0] DATA_0,
  output [15:0] DATA_1
);

  wire and_1_out, d_ff_1_q, demultiplexer_1_out0, demultiplexer_1_out1, demultiplexer_1_out2,
       demultiplexer_1_out3, demultiplexer_1_out4, demultiplexer_1_out5, demultiplexer_1_out6,
       demultiplexer_1_out7, demultiplexer_1_out8, demultiplexer_1_out9, demultiplexer_1_out10,
       demultiplexer_1_out11, demultiplexer_1_out12, demultiplexer_1_out13, demultiplexer_1_out14,
       demultiplexer_1_out15, demultiplexer_1_out16, demultiplexer_1_out17, demultiplexer_1_out18,
       demultiplexer_1_out19, demultiplexer_1_out20, demultiplexer_1_out21, demultiplexer_1_out22,
       demultiplexer_1_out23, demultiplexer_1_out24, demultiplexer_1_out25, demultiplexer_1_out26,
       demultiplexer_1_out27, demultiplexer_1_out28, demultiplexer_1_out29, demultiplexer_1_out30,
       demultiplexer_1_out31;
  wire [4:0] register_2_q, register_3_q, register_4_q;
  wire [15:0] register_1_q, register_5_q, register_6_q, register_7_q, register_8_q, register_9_q,
       register_10_q, register_11_q, register_12_q, register_13_q, register_14_q, register_15_q,
       register_16_q, register_17_q, register_18_q, register_19_q, register_20_q, register_21_q,
       register_22_q, register_23_q, register_24_q, register_25_q, register_26_q, register_27_q,
       register_28_q, register_29_q, register_30_q, register_31_q, register_32_q, register_33_q,
       register_34_q, register_35_q, register_36_q;

  D_Flip_Flop d_ff_1 (.D(WRITE), .clk(CLK), .Q(d_ff_1_q));  // open: Qn, preset, reset
  Register #(.width(16)) register_1 (.D(DATA_IN), .en(1'b1), .clk(CLK), .Q(register_1_q));  // open: clr
  Register #(.width(5)) register_2 (.D(WRITE_ADRESS), .en(1'b1), .clk(CLK), .Q(register_2_q));  // open: clr
  Register #(.width(5)) register_3 (.D(READ_0), .en(1'b1), .clk(CLK), .Q(register_3_q));  // open: clr
  Register #(.width(5)) register_4 (.D(READ_1), .en(1'b1), .clk(CLK), .Q(register_4_q));  // open: clr
  Register #(.width(16)) register_5 (
    .D({16{1'b0}}), .en(1'b1), .clk(demultiplexer_1_out0), .Q(register_5_q));  // open: clr
  and and_1 (and_1_out, d_ff_1_q, CLK, 1'b1);
  Demultiplexer #(.select(5)) demultiplexer_1 (
    .out0(demultiplexer_1_out0), .out1(demultiplexer_1_out1), .out2(demultiplexer_1_out2),
    .out3(demultiplexer_1_out3), .out4(demultiplexer_1_out4), .out5(demultiplexer_1_out5),
    .out6(demultiplexer_1_out6), .out7(demultiplexer_1_out7), .out8(demultiplexer_1_out8),
    .out9(demultiplexer_1_out9), .out10(demultiplexer_1_out10), .out11(demultiplexer_1_out11),
    .out12(demultiplexer_1_out12), .out13(demultiplexer_1_out13), .out14(demultiplexer_1_out14),
    .out15(demultiplexer_1_out15), .out16(demultiplexer_1_out16), .out17(demultiplexer_1_out17),
    .out18(demultiplexer_1_out18), .out19(demultiplexer_1_out19), .out20(demultiplexer_1_out20),
    .out21(demultiplexer_1_out21), .out22(demultiplexer_1_out22), .out23(demultiplexer_1_out23),
    .out24(demultiplexer_1_out24), .out25(demultiplexer_1_out25), .out26(demultiplexer_1_out26),
    .out27(demultiplexer_1_out27), .out28(demultiplexer_1_out28), .out29(demultiplexer_1_out29),
    .out30(demultiplexer_1_out30), .out31(demultiplexer_1_out31), .in(and_1_out), .sel(register_2_q));
  Register #(.width(16)) register_6 (
    .D(register_1_q), .en(1'b1), .clk(demultiplexer_1_out1), .Q(register_6_q));  // open: clr
  Register #(.width(16)) register_7 (
    .D(register_1_q), .en(1'b1), .clk(demultiplexer_1_out2), .Q(register_7_q));  // open: clr
  Register #(.width(16)) register_8 (
    .D(register_1_q), .en(1'b1), .clk(demultiplexer_1_out3), .Q(register_8_q));  // open: clr
  Register #(.width(16)) register_9 (
    .D(register_1_q), .en(1'b1), .clk(demultiplexer_1_out4), .Q(register_9_q));  // open: clr
  Register #(.width(16)) register_10 (
    .D(register_1_q), .en(1'b1), .clk(demultiplexer_1_out5), .Q(register_10_q));  // open: clr
  Register #(.width(16)) register_11 (
    .D(register_1_q), .en(1'b1), .clk(demultiplexer_1_out6), .Q(register_11_q));  // open: clr
  Register #(.width(16)) register_12 (
    .D(register_1_q), .en(1'b1), .clk(demultiplexer_1_out7), .Q(register_12_q));  // open: clr
  Register #(.width(16)) register_13 (
    .D(register_1_q), .en(1'b1), .clk(demultiplexer_1_out8), .Q(register_13_q));  // open: clr
  Register #(.width(16)) register_14 (
    .D(register_1_q), .en(1'b1), .clk(demultiplexer_1_out9), .Q(register_14_q));  // open: clr
  Register #(.width(16)) register_15 (
    .D(register_1_q), .en(1'b1), .clk(demultiplexer_1_out10), .Q(register_15_q));  // open: clr
  Register #(.width(16)) register_16 (
    .D(register_1_q), .en(1'b1), .clk(demultiplexer_1_out11), .Q(register_16_q));  // open: clr
  Register #(.width(16)) register_17 (
    .D(register_1_q), .en(1'b1), .clk(demultiplexer_1_out12), .Q(register_17_q));  // open: clr
  Register #(.width(16)) register_18 (
    .D(register_1_q), .en(1'b1), .clk(demultiplexer_1_out13), .Q(register_18_q));  // open: clr
  Register #(.width(16)) register_19 (
    .D(register_1_q), .en(1'b1), .clk(demultiplexer_1_out14), .Q(register_19_q));  // open: clr
  Register #(.width(16)) register_20 (
    .D(register_1_q), .en(1'b1), .clk(demultiplexer_1_out15), .Q(register_20_q));  // open: clr
  Register #(.width(16)) register_21 (
    .D(register_1_q), .en(1'b1), .clk(demultiplexer_1_out16), .Q(register_21_q));  // open: clr
  Register #(.width(16)) register_22 (
    .D(register_1_q), .en(1'b1), .clk(demultiplexer_1_out17), .Q(register_22_q));  // open: clr
  Register #(.width(16)) register_23 (
    .D(register_1_q), .en(1'b1), .clk(demultiplexer_1_out18), .Q(register_23_q));  // open: clr
  Register #(.width(16)) register_24 (
    .D(register_1_q), .en(1'b1), .clk(demultiplexer_1_out19), .Q(register_24_q));  // open: clr
  Register #(.width(16)) register_25 (
    .D(register_1_q), .en(1'b1), .clk(demultiplexer_1_out20), .Q(register_25_q));  // open: clr
  Register #(.width(16)) register_26 (
    .D(register_1_q), .en(1'b1), .clk(demultiplexer_1_out21), .Q(register_26_q));  // open: clr
  Register #(.width(16)) register_27 (
    .D(register_1_q), .en(1'b1), .clk(demultiplexer_1_out22), .Q(register_27_q));  // open: clr
  Register #(.width(16)) register_28 (
    .D(register_1_q), .en(1'b1), .clk(demultiplexer_1_out23), .Q(register_28_q));  // open: clr
  Register #(.width(16)) register_29 (
    .D(register_1_q), .en(1'b1), .clk(demultiplexer_1_out24), .Q(register_29_q));  // open: clr
  Register #(.width(16)) register_30 (
    .D(register_1_q), .en(1'b1), .clk(demultiplexer_1_out25), .Q(register_30_q));  // open: clr
  Register #(.width(16)) register_31 (
    .D(register_1_q), .en(1'b1), .clk(demultiplexer_1_out26), .Q(register_31_q));  // open: clr
  Register #(.width(16)) register_32 (
    .D(register_1_q), .en(1'b1), .clk(demultiplexer_1_out27), .Q(register_32_q));  // open: clr
  Register #(.width(16)) register_33 (
    .D(register_1_q), .en(1'b1), .clk(demultiplexer_1_out28), .Q(register_33_q));  // open: clr
  Register #(.width(16)) register_34 (
    .D(register_1_q), .en(1'b1), .clk(demultiplexer_1_out29), .Q(register_34_q));  // open: clr
  Register #(.width(16)) register_35 (
    .D(register_1_q), .en(1'b1), .clk(demultiplexer_1_out30), .Q(register_35_q));  // open: clr
  Multiplexer #(.select(5), .width(16)) multiplexer_1 (
    .in0(register_5_q), .in1(register_6_q), .in2(register_7_q), .in3(register_8_q), .in4(register_9_q),
    .in5(register_10_q), .in6(register_11_q), .in7(register_12_q), .in8(register_13_q), .in9(register_14_q),
    .in10(register_15_q), .in11(register_16_q), .in12(register_17_q), .in13(register_18_q),
    .in14(register_19_q), .in15(register_20_q), .in16(register_21_q), .in17(register_22_q),
    .in18(register_23_q), .in19(register_24_q), .in20(register_25_q), .in21(register_26_q),
    .in22(register_27_q), .in23(register_28_q), .in24(register_29_q), .in25(register_30_q),
    .in26(register_31_q), .in27(register_32_q), .in28(register_33_q), .in29(register_34_q),
    .in30(register_35_q), .in31(register_36_q), .out(DATA_0), .sel(register_3_q));
  Register #(.width(16)) register_36 (
    .D(register_1_q), .en(1'b1), .clk(demultiplexer_1_out31), .Q(register_36_q));  // open: clr
  Multiplexer #(.select(5), .width(16)) multiplexer_2 (
    .in0(register_5_q), .in1(register_6_q), .in2(register_7_q), .in3(register_8_q), .in4(register_9_q),
    .in5(register_10_q), .in6(register_11_q), .in7(register_12_q), .in8(register_13_q), .in9(register_14_q),
    .in10(register_15_q), .in11(register_16_q), .in12(register_17_q), .in13(register_18_q),
    .in14(register_19_q), .in15(register_20_q), .in16(register_21_q), .in17(register_22_q),
    .in18(register_23_q), .in19(register_24_q), .in20(register_25_q), .in21(register_26_q),
    .in22(register_27_q), .in23(register_28_q), .in24(register_29_q), .in25(register_30_q),
    .in26(register_31_q), .in27(register_32_q), .in28(register_33_q), .in29(register_34_q),
    .in30(register_35_q), .in31(register_36_q), .out(DATA_1), .sel(register_4_q));
endmodule
