// Logisim project Adress_Comparator_10bit.circ as structural Verilog: 1 circuit, main circuit Adress_Comparator_10bit
module Adress_Comparator_10bit (
  input  [9:0] ADRESS,
  input  [9:0] PHYSICAL_ADRESS,
  output OUTPUT_ADRESS
);

  wire or_1_out, or_2_out, or_3_out, or_4_out, or_5_out, or_6_out, or_7_out, or_8_out, or_9_out;
  wire [9:0] xor_1_out;

  assign xor_1_out = ADRESS ^ PHYSICAL_ADRESS;  // XOR_Gate xor_1, 10 bits wide
  or or_1 (or_1_out, xor_1_out[9], xor_1_out[8]);
  or or_2 (or_2_out, xor_1_out[7], xor_1_out[6]);
  or or_3 (or_3_out, or_1_out, or_2_out);
  or or_4 (or_4_out, xor_1_out[5], xor_1_out[4]);
  or or_5 (or_5_out, or_3_out, or_9_out);
  or or_6 (or_6_out, xor_1_out[3], xor_1_out[2]);
  or or_7 (or_7_out, or_4_out, or_6_out);
  not not_1 (OUTPUT_ADRESS, or_5_out);
  or or_8 (or_8_out, xor_1_out[1], xor_1_out[0]);
  or or_9 (or_9_out, or_7_out, or_8_out);
endmodule
