// Logisim project Adress_Comparator_4bit.circ as structural Verilog: 1 circuit, main circuit Adress_Comparator_4bit
module Adress_Comparator_4bit (
  input  [3:0] ADRESS,
  input  [3:0] PHYSICAL_ADRESS,
  output OUTPUT_ADRESS
);

  wire or_1_out, or_2_out, or_3_out;
  wire [3:0] xor_1_out;

  assign xor_1_out = ADRESS ^ PHYSICAL_ADRESS;  // XOR_Gate xor_1, 4 bits wide
  or or_1 (or_1_out, xor_1_out[3], xor_1_out[2]);
  or or_2 (or_2_out, or_1_out, or_3_out);
  or or_3 (or_3_out, xor_1_out[1], xor_1_out[0]);
  not not_1 (OUTPUT_ADRESS, or_2_out);
endmodule
