// Logisim project Adress_Comparator_5bit.circ as structural Verilog: 1 circuit, main circuit Adress_Comparator_5bit
module Adress_Comparator_5bit (
  input  [4:0] ADRESS,
  input  [4:0] PHYSICAL_ADRESS,
  output OUTPUT_ADRESS
);

  wire or_1_out, or_2_out, or_3_out, or_4_out;
  wire [4:0] xor_1_out;

  assign xor_1_out = ADRESS ^ PHYSICAL_ADRESS;  // XOR_Gate xor_1, 5 bits wide
  or or_1 (or_1_out, xor_1_out[4], xor_1_out[3]);
  or or_2 (or_2_out, or_1_out, or_3_out);
  or or_3 (or_3_out, xor_1_out[2], xor_1_out[1]);
  or or_4 (or_4_out, xor_1_out[0], or_2_out);
  not not_1 (OUTPUT_ADRESS, or_4_out);
endmodule
