// Logisim project Stack.circ as structural Verilog: 1 circuit, main circuit Stack
module Stack (
  input  RESET,
  input  PUSH,
  input  POP,
  input  CLK,
  input  READ,
  input  [15:0] DATA_IN,
  output [15:0] OUTPUT_STACK
);

  wire adress_comparator_10bit_1_output_adress, and_1_out, and_2_out, and_3_out, and_4_out, and_5_out,
       and_6_out, and_7_out, and_8_out, d_ff_1_q, d_ff_2_q, d_ff_3_q, not_1_out, not_2_out, xor_1_out;
  wire [1:0] multiplexer_2_out, multiplexer_3_out, or_1_out;
  wire [9:0] adder_1_out, multiplexer_4_out, register_2_q, register_3_q, register_4_q, subtractor_1_out;
  wire [15:0] multiplexer_1_out, ram_1_dout, register_1_q;

  D_Flip_Flop d_ff_1 (.D(RESET), .clk(CLK), .Q(d_ff_1_q), .reset(d_ff_1_q));  // open: Qn, preset
  D_Flip_Flop d_ff_2 (.D(PUSH), .clk(CLK), .Q(d_ff_2_q), .reset(d_ff_1_q));  // open: Qn, preset
  D_Flip_Flop d_ff_3 (.D(POP), .clk(CLK), .Q(d_ff_3_q), .reset(d_ff_1_q));  // open: Qn, preset
  Register #(.width(16)) register_1 (.D(DATA_IN), .en(1'b1), .clk(CLK), .Q(register_1_q));  // open: clr
  and and_1 (and_1_out, d_ff_1_q, CLK);
  and and_2 (and_2_out, d_ff_2_q, CLK);
  and and_3 (and_3_out, d_ff_3_q, CLK);
  Multiplexer #(.width(16)) multiplexer_1 (.in0({16{1'b0}}), .in1(register_1_q), .out(multiplexer_1_out), .sel(CLK));
  xor xor_1 (xor_1_out, and_2_out, and_3_out);
  and and_4 (and_4_out, and_1_out, CLK);
  and and_5 (and_5_out, xor_1_out, CLK);
  and and_6 (and_6_out, and_2_out, xor_1_out);
  and and_7 (and_7_out, and_3_out, xor_1_out);
  Multiplexer #(.width(2)) multiplexer_2 (.in0(2'b00), .in1(2'b01), .out(multiplexer_2_out), .sel(and_6_out));
  Multiplexer #(.width(2)) multiplexer_3 (.in0(2'b00), .in1(2'b10), .out(multiplexer_3_out), .sel(and_7_out));
  not not_1 (not_1_out, adress_comparator_10bit_1_output_adress);
  assign or_1_out = multiplexer_2_out | multiplexer_3_out;  // OR_Gate or_1, 2 bits wide
  and and_8 (and_8_out, not_1_out, and_5_out);
  Adress_Comparator_10bit adress_comparator_10bit_1 (
    .ADRESS(multiplexer_4_out), .PHYSICAL_ADRESS(register_2_q),
    .OUTPUT_ADRESS(adress_comparator_10bit_1_output_adress));
  Multiplexer #(.select(2), .width(10)) multiplexer_4 (
    .in0(register_2_q), .in1(register_4_q), .in2(register_3_q), .in3(register_2_q), .out(multiplexer_4_out),
    .sel(or_1_out));
  RAM #(.addrWidth(10), .clearpin("true"), .dataWidth(16), .enables("line")) ram_1 (
    .addr(register_2_q), .we(and_6_out), .clk(not_2_out), .din(multiplexer_1_out), .dout(ram_1_dout),
    .clr(and_4_out));
  not not_2 (not_2_out, and_8_out);
  Register #(.width(10)) register_2 (
    .D(multiplexer_4_out), .en(1'b1), .clk(and_8_out), .Q(register_2_q), .clr(and_4_out));
  Subtractor #(.width(10)) subtractor_1 (
    .a(register_2_q), .b({10{1'b0}}), .out(subtractor_1_out), .bin(1'b1));  // open: bout
  Adder #(.width(10)) adder_1 (.a(register_2_q), .b({10{1'b0}}), .out(adder_1_out), .cin(1'b1));  // open: cout
  Register #(.width(10)) register_3 (.D(subtractor_1_out), .en(1'b1), .clk(and_5_out), .Q(register_3_q));  // open: clr
  Register #(.width(10)) register_4 (.D(adder_1_out), .en(1'b1), .clk(and_5_out), .Q(register_4_q));  // open: clr
  Multiplexer #(.width(16)) multiplexer_5 (.in0({16{1'b0}}), .in1(ram_1_dout), .out(OUTPUT_STACK), .sel(READ));
endmodule
